// Digital circuit plantilla(1).dig as structural Verilog
module plantilla_1 (
  input  [4:0] N1,
  input  [4:0] N2,
  input  [4:0] N3,
  input  [4:0] N4,
  input  [4:0] N5,
  input  [4:0] N6,
  input  [4:0] N7,
  input  [4:0] N8,
  input  [4:0] N9,
  input  [4:0] N10,
  input  plus,
  output out_12
);

  wire add_2_s;
  wire [4:0] neg_1_out, neg_2_out, neg_3_out, neg_4_out, neg_5_out, neg_11_out, neg_12_out, neg_13_out,
       neg_14_out, neg_15_out;
  wire [7:0] multiplexer_11_out, multiplexer_12_out, multiplexer_13_out, N1_t, N2_t, N3_t, N4_t, N5_t, N6_t,
       N7_t, N8_t, N9_t, N10_t, neg_6_out, neg_7_out, neg_8_out, neg_9_out, neg_10_out, neg_16_out,
       neg_17_out, neg_18_out, neg_19_out, neg_20_out;

  Neg #(.Bits(5)) neg_1 (.in(N2), .out(neg_1_out));
  Neg #(.Bits(5)) neg_2 (.in(N3), .out(neg_2_out));
  Neg #(.Bits(5)) neg_3 (.in(N5), .out(neg_3_out));
  Neg #(.Bits(5)) neg_4 (.in(N1), .out(neg_4_out));
  Neg #(.Bits(5)) neg_5 (.in(N5), .out(neg_5_out));
  Neg #(.Bits(8)) neg_6 (.in({3'b000, neg_4_out}), .out(neg_6_out));
  Neg #(.Bits(8)) neg_7 (.in({3'b000, neg_1_out}), .out(neg_7_out));
  Neg #(.Bits(8)) neg_8 (.in({3'b000, neg_2_out}), .out(neg_8_out));
  Neg #(.Bits(8)) neg_9 (.in({3'b000, neg_3_out}), .out(neg_9_out));
  Neg #(.Bits(8)) neg_10 (.in({3'b000, neg_5_out}), .out(neg_10_out));
  Multiplexer #(.Bits(8)) multiplexer_1 (.sel(N2[4]), .in_0({3'b000, N2}), .in_1(neg_7_out), .out(N2_t));
  Multiplexer #(.Bits(8)) multiplexer_2 (.sel(N3[4]), .in_0({3'b000, N3}), .in_1(neg_8_out), .out(N3_t));
  Multiplexer #(.Bits(8)) multiplexer_3 (.sel(N5[4]), .in_0({3'b000, N5}), .in_1(neg_9_out), .out(N4_t));
  Multiplexer #(.Bits(8)) multiplexer_4 (.sel(N5[4]), .in_0({3'b000, N5}), .in_1(neg_10_out), .out(N5_t));
  Multiplexer #(.Bits(8)) multiplexer_5 (.sel(N1[4]), .in_0({3'b000, N1}), .in_1(neg_6_out), .out(N1_t));
  Neg #(.Bits(5)) neg_11 (.in(N7), .out(neg_11_out));
  Neg #(.Bits(5)) neg_12 (.in(N8), .out(neg_12_out));
  Neg #(.Bits(5)) neg_13 (.in(N9), .out(neg_13_out));
  Neg #(.Bits(5)) neg_14 (.in(N10), .out(neg_14_out));
  Neg #(.Bits(5)) neg_15 (.in(N6), .out(neg_15_out));
  Neg #(.Bits(8)) neg_16 (.in({3'b000, neg_11_out}), .out(neg_16_out));
  Neg #(.Bits(8)) neg_17 (.in({3'b000, neg_12_out}), .out(neg_17_out));
  Neg #(.Bits(8)) neg_18 (.in({3'b000, neg_13_out}), .out(neg_18_out));
  Neg #(.Bits(8)) neg_19 (.in({3'b000, neg_15_out}), .out(neg_19_out));
  Neg #(.Bits(8)) neg_20 (.in({3'b000, neg_14_out}), .out(neg_20_out));
  Multiplexer #(.Bits(8)) multiplexer_6 (.sel(N6[4]), .in_0({3'b000, N6}), .in_1(neg_19_out), .out(N6_t));
  Multiplexer #(.Bits(8)) multiplexer_7 (.sel(N7[4]), .in_0({3'b000, N7}), .in_1(neg_16_out), .out(N7_t));
  Multiplexer #(.Bits(8)) multiplexer_8 (.sel(N8[4]), .in_0({3'b000, N8}), .in_1(neg_17_out), .out(N8_t));
  Multiplexer #(.Bits(8)) multiplexer_9 (.sel(N9[4]), .in_0({3'b000, N9}), .in_1(neg_18_out), .out(N9_t));
  Multiplexer #(.Bits(8)) multiplexer_10 (.sel(N10[4]), .in_0({3'b000, N10}), .in_1(neg_20_out), .out(N10_t));
  Multiplexer #(.Bits(8)) multiplexer_11 (.sel(N3_t[7]), .in_0(N3_t), .in_1({8{1'b0}}), .out(multiplexer_11_out));
  Multiplexer #(.Bits(8)) multiplexer_12 (.sel(N1_t[7]), .in_0(N1_t), .in_1({8{1'b0}}), .out(multiplexer_12_out));
  Multiplexer #(.Bits(8)) multiplexer_13 (.sel(N2_t[7]), .in_0(N2_t), .in_1({8{1'b0}}), .out(multiplexer_13_out));
  Add add_1 (.a(add_2_s), .b(multiplexer_11_out[0]), .c_i(1'b0));  // open: s, c_o
  Add add_2 (.a(multiplexer_12_out[0]), .b(multiplexer_13_out[0]), .c_i(1'b0), .s(add_2_s));  // open: c_o
  // Pins of 1 and 8 bits meet at multiplexer_12_out
  // Pins of 1 and 8 bits meet at multiplexer_13_out
  // Pins of 1 and 8 bits meet at multiplexer_11_out

  // Notes on the sheet:
  //   SUMA DE POSITIVOS
endmodule
