// Digital circuit plantilla.dig as structural Verilog
module plantilla (
  input  [4:0] N1,
  input  [4:0] N2,
  input  [4:0] N3,
  input  [4:0] N4,
  input  [4:0] N5,
  input  [4:0] N6,
  input  [4:0] N7,
  input  [4:0] N8,
  input  [4:0] N9,
  input  [4:0] N10,
  input  plus,
  output [7:0] out_12,
  output [7:0] out_13
);

  wire not_1_out;
  wire [4:0] neg_1_out, neg_2_out, neg_3_out, neg_4_out, neg_5_out, neg_6_out, neg_7_out, neg_8_out,
       neg_9_out, neg_10_out;
  wire [7:0] add_1_s, add_2_s, add_3_s, add_4_s, add_5_s, add_6_s, add_7_s, add_8_s, add_9_s, add_10_s,
       add_11_s, add_12_s, add_13_s, add_14_s, add_15_s, add_16_s, add_17_s, add_18_s, multiplexer_11_out,
       multiplexer_12_out, multiplexer_13_out, multiplexer_14_out, multiplexer_15_out, multiplexer_16_out,
       multiplexer_17_out, multiplexer_18_out, multiplexer_19_out, multiplexer_20_out, multiplexer_21_out,
       multiplexer_22_out, multiplexer_23_out, multiplexer_24_out, multiplexer_25_out, multiplexer_26_out,
       multiplexer_27_out, multiplexer_28_out, multiplexer_29_out, multiplexer_30_out, multiplexer_32_out,
       n1_t, n2_t, n3_t, n4_t, n5_t, n6_t, n7_t, n8_t, n9_t, n10_t, neg_11_out, neg_12_out, neg_13_out,
       neg_14_out, neg_15_out, neg_16_out, neg_17_out, neg_18_out, neg_19_out, neg_20_out;

  Neg #(.Bits(5)) neg_1 (.in(N1), .out(neg_1_out));
  Neg #(.Bits(5)) neg_2 (.in(N2), .out(neg_2_out));
  Neg #(.Bits(5)) neg_3 (.in(N3), .out(neg_3_out));
  Neg #(.Bits(5)) neg_4 (.in(N4), .out(neg_4_out));
  Neg #(.Bits(5)) neg_5 (.in(N5), .out(neg_5_out));
  Neg #(.Bits(5)) neg_6 (.in(N6), .out(neg_6_out));
  Neg #(.Bits(5)) neg_7 (.in(N7), .out(neg_7_out));
  Neg #(.Bits(5)) neg_8 (.in(N8), .out(neg_8_out));
  Neg #(.Bits(5)) neg_9 (.in(N9), .out(neg_9_out));
  Neg #(.Bits(5)) neg_10 (.in(N10), .out(neg_10_out));
  Neg #(.Bits(8)) neg_11 (.in({3'b000, neg_1_out}), .out(neg_11_out));
  Neg #(.Bits(8)) neg_12 (.in({3'b000, neg_2_out}), .out(neg_12_out));
  Neg #(.Bits(8)) neg_13 (.in({3'b000, neg_3_out}), .out(neg_13_out));
  Neg #(.Bits(8)) neg_14 (.in({3'b000, neg_4_out}), .out(neg_14_out));
  Neg #(.Bits(8)) neg_15 (.in({3'b000, neg_5_out}), .out(neg_15_out));
  Neg #(.Bits(8)) neg_16 (.in({3'b000, neg_6_out}), .out(neg_16_out));
  Neg #(.Bits(8)) neg_17 (.in({3'b000, neg_7_out}), .out(neg_17_out));
  Neg #(.Bits(8)) neg_18 (.in({3'b000, neg_8_out}), .out(neg_18_out));
  Neg #(.Bits(8)) neg_19 (.in({3'b000, neg_9_out}), .out(neg_19_out));
  Neg #(.Bits(8)) neg_20 (.in({3'b000, neg_10_out}), .out(neg_20_out));
  Multiplexer #(.Bits(8)) multiplexer_1 (.sel(N1[4]), .in_0({3'b000, N1}), .in_1(neg_11_out), .out(n1_t));
  Multiplexer #(.Bits(8)) multiplexer_2 (.sel(N2[4]), .in_0({3'b000, N2}), .in_1(neg_12_out), .out(n2_t));
  Multiplexer #(.Bits(8)) multiplexer_3 (.sel(N3[4]), .in_0({3'b000, N3}), .in_1(neg_13_out), .out(n3_t));
  Multiplexer #(.Bits(8)) multiplexer_4 (.sel(N4[4]), .in_0({3'b000, N4}), .in_1(neg_14_out), .out(n4_t));
  Multiplexer #(.Bits(8)) multiplexer_5 (.sel(N5[4]), .in_0({3'b000, N5}), .in_1(neg_15_out), .out(n5_t));
  Multiplexer #(.Bits(8)) multiplexer_6 (.sel(N6[4]), .in_0({3'b000, N6}), .in_1(neg_16_out), .out(n6_t));
  Multiplexer #(.Bits(8)) multiplexer_7 (.sel(N7[4]), .in_0({3'b000, N7}), .in_1(neg_17_out), .out(n7_t));
  Multiplexer #(.Bits(8)) multiplexer_8 (.sel(N8[4]), .in_0({3'b000, N8}), .in_1(neg_18_out), .out(n8_t));
  Multiplexer #(.Bits(8)) multiplexer_9 (.sel(N9[4]), .in_0({3'b000, N9}), .in_1(neg_19_out), .out(n9_t));
  Multiplexer #(.Bits(8)) multiplexer_10 (.sel(N10[4]), .in_0({3'b000, N10}), .in_1(neg_20_out), .out(n10_t));
  Multiplexer #(.Bits(8)) multiplexer_11 (.sel(n1_t[7]), .in_0(n1_t), .in_1({8{1'b0}}), .out(multiplexer_11_out));
  Multiplexer #(.Bits(8)) multiplexer_12 (.sel(n2_t[7]), .in_0(n2_t), .in_1({8{1'b0}}), .out(multiplexer_12_out));
  Multiplexer #(.Bits(8)) multiplexer_13 (.sel(n3_t[7]), .in_0(n3_t), .in_1({8{1'b0}}), .out(multiplexer_13_out));
  Multiplexer #(.Bits(8)) multiplexer_14 (.sel(n4_t[7]), .in_0(n4_t), .in_1({8{1'b0}}), .out(multiplexer_14_out));
  Multiplexer #(.Bits(8)) multiplexer_15 (.sel(n5_t[7]), .in_0(n5_t), .in_1({8{1'b0}}), .out(multiplexer_15_out));
  Multiplexer #(.Bits(8)) multiplexer_16 (.sel(n6_t[7]), .in_0(n6_t), .in_1({8{1'b0}}), .out(multiplexer_16_out));
  Multiplexer #(.Bits(8)) multiplexer_17 (.sel(n7_t[7]), .in_0(n7_t), .in_1({8{1'b0}}), .out(multiplexer_17_out));
  Multiplexer #(.Bits(8)) multiplexer_18 (.sel(n8_t[7]), .in_0(n8_t), .in_1({8{1'b0}}), .out(multiplexer_18_out));
  Multiplexer #(.Bits(8)) multiplexer_19 (.sel(n9_t[7]), .in_0(n9_t), .in_1({8{1'b0}}), .out(multiplexer_19_out));
  Multiplexer #(.Bits(8)) multiplexer_20 (.sel(n10_t[7]), .in_0(n10_t), .in_1({8{1'b0}}), .out(multiplexer_20_out));
  Multiplexer #(.Bits(8)) multiplexer_21 (.sel(n1_t[7]), .in_0({8{1'b0}}), .in_1(n1_t), .out(multiplexer_21_out));
  Multiplexer #(.Bits(8)) multiplexer_22 (.sel(n2_t[7]), .in_0({8{1'b0}}), .in_1(n2_t), .out(multiplexer_22_out));
  Multiplexer #(.Bits(8)) multiplexer_23 (.sel(n3_t[7]), .in_0({8{1'b0}}), .in_1(n3_t), .out(multiplexer_23_out));
  Multiplexer #(.Bits(8)) multiplexer_24 (.sel(n4_t[7]), .in_0({8{1'b0}}), .in_1(n4_t), .out(multiplexer_24_out));
  Multiplexer #(.Bits(8)) multiplexer_25 (.sel(n5_t[7]), .in_0({8{1'b0}}), .in_1(n5_t), .out(multiplexer_25_out));
  Multiplexer #(.Bits(8)) multiplexer_26 (.sel(n6_t[7]), .in_0({8{1'b0}}), .in_1(n6_t), .out(multiplexer_26_out));
  Multiplexer #(.Bits(8)) multiplexer_27 (.sel(n7_t[7]), .in_0({8{1'b0}}), .in_1(n7_t), .out(multiplexer_27_out));
  Multiplexer #(.Bits(8)) multiplexer_28 (.sel(n8_t[7]), .in_0({8{1'b0}}), .in_1(n8_t), .out(multiplexer_28_out));
  Multiplexer #(.Bits(8)) multiplexer_29 (.sel(n9_t[7]), .in_0({8{1'b0}}), .in_1(n9_t), .out(multiplexer_29_out));
  Multiplexer #(.Bits(8)) multiplexer_30 (.sel(n10_t[7]), .in_0({8{1'b0}}), .in_1(n10_t), .out(multiplexer_30_out));
  Add #(.Bits(8)) add_1 (.a(multiplexer_11_out), .b(multiplexer_12_out), .c_i(1'b0), .s(add_1_s));  // open: c_o
  Add #(.Bits(8)) add_2 (.a(multiplexer_13_out), .b(multiplexer_14_out), .c_i(1'b0), .s(add_2_s));  // open: c_o
  Add #(.Bits(8)) add_3 (.a(multiplexer_15_out), .b(multiplexer_16_out), .c_i(1'b0), .s(add_3_s));  // open: c_o
  Add #(.Bits(8)) add_4 (.a(multiplexer_17_out), .b(multiplexer_18_out), .c_i(1'b0), .s(add_4_s));  // open: c_o
  Add #(.Bits(8)) add_5 (.a(multiplexer_19_out), .b(multiplexer_20_out), .c_i(1'b0), .s(add_5_s));  // open: c_o
  Add #(.Bits(8)) add_6 (.a(multiplexer_21_out), .b(multiplexer_22_out), .c_i(1'b0), .s(add_6_s));  // open: c_o
  Add #(.Bits(8)) add_7 (.a(multiplexer_23_out), .b(multiplexer_24_out), .c_i(1'b0), .s(add_7_s));  // open: c_o
  Add #(.Bits(8)) add_8 (.a(multiplexer_25_out), .b(multiplexer_26_out), .c_i(1'b0), .s(add_8_s));  // open: c_o
  Add #(.Bits(8)) add_9 (.a(multiplexer_27_out), .b(multiplexer_28_out), .c_i(1'b0), .s(add_9_s));  // open: c_o
  Add #(.Bits(8)) add_10 (.a(multiplexer_29_out), .b(multiplexer_30_out), .c_i(1'b0), .s(add_10_s));  // open: c_o
  Add #(.Bits(8)) add_11 (.a(add_1_s), .b(add_2_s), .c_i(1'b0), .s(add_11_s));  // open: c_o
  Add #(.Bits(8)) add_12 (.a(add_3_s), .b(add_4_s), .c_i(1'b0), .s(add_12_s));  // open: c_o
  Add #(.Bits(8)) add_13 (.a(add_6_s), .b(add_7_s), .c_i(1'b0), .s(add_13_s));  // open: c_o
  Add #(.Bits(8)) add_14 (.a(add_8_s), .b(add_9_s), .c_i(1'b0), .s(add_14_s));  // open: c_o
  Add #(.Bits(8)) add_15 (.a(add_11_s), .b(add_12_s), .c_i(1'b0), .s(add_15_s));  // open: c_o
  Add #(.Bits(8)) add_16 (.a(add_13_s), .b(add_14_s), .c_i(1'b0), .s(add_16_s));  // open: c_o
  Add #(.Bits(8)) add_17 (.a(add_15_s), .b(add_5_s), .c_i(1'b0), .s(add_17_s));  // open: c_o
  Add #(.Bits(8)) add_18 (.a(add_16_s), .b(add_10_s), .c_i(1'b0), .s(add_18_s));  // open: c_o
  not not_1 (not_1_out, plus);
  Multiplexer #(.Bits(8)) multiplexer_31 (.sel(not_1_out), .in_0(add_17_s), .in_1({8{1'b0}}), .out(out_12));
  Multiplexer #(.Bits(8)) multiplexer_32 (.sel(plus), .in_0(add_18_s), .in_1({8{1'b0}}), .out(multiplexer_32_out));
  Neg #(.Bits(8)) neg_21 (.in(multiplexer_32_out), .out(out_13));

  // Other names for the same wires on the sheet: Signo = plus
endmodule
