// Digital circuit Prueba Diseño de Sistemas Lógicos.dig as structural Verilog
module \Prueba_Diseño_de_Sistemas_Lógicos  (
  input  LS10,
  input  S11,
  input  S12,
  input  S13,
  input  MS14,
  input  LS20,
  input  S21,
  input  S22,
  input  S23,
  input  MS24,
  input  Out0,
  input  Out1,
  input  Out2,
  input  LS90,
  input  S91,
  input  S92,
  input  MS93,
  input  LS30,
  input  S31,
  input  S32,
  input  MS33,
  input  LS30_2,
  input  S31_2,
  input  S32_2,
  input  S33,
  input  MS34,
  input  LS40,
  input  S41,
  input  S42,
  input  S43,
  input  MS44,
  input  LS50,
  input  S51,
  input  S52,
  input  S53,
  input  MS54,
  input  LS60,
  input  S61,
  input  S62,
  input  S63,
  input  MS64,
  input  [4:0] in_42
);

  wire and_1_out, comparator_1_gt, comparator_2_lt;
  wire [0:0] and_2_out;
  wire [4:0] neg_1_out;

  Neg #(.Bits(5)) neg_1 (.in(in_42), .out(neg_1_out));
  Comparator #(.Bits(5)) comparator_1 (.a(neg_1_out), .b(5'b00011), .gt(comparator_1_gt));  // open: eq, lt
  Comparator #(.Bits(5)) comparator_2 (.a(neg_1_out), .b(5'b01001), .lt(comparator_2_lt));  // open: gt, eq
  and and_1 (and_1_out, comparator_1_gt, comparator_2_lt);
  and and_2 (and_2_out[0], and_1_out, in_42[4]);
  Add #(.Bits(3)) add_1 (.a({2'b00, and_2_out[0]}), .c_i(1'b0));  // open: b, s, c_o
endmodule
