// Digital circuit Ejercicio7segmentos.dig as structural Verilog
module Ejercicio7segmentos (
  input  [4:0] in_1,
  input  HEX
);

  wire A2, a2_t, and_1_out, and_2_out, and_3_out, and_4_out, and_5_out, and_6_out, and_7_out, and_8_out,
       and_9_out, and_10_out, and_11_out, and_12_out, and_13_out, and_14_out, and_15_out, and_16_out,
       and_17_out, and_18_out, and_19_out, and_20_out, and_21_out, and_22_out, and_23_out, and_24_out,
       and_25_out, and_26_out, and_27_out, and_28_out, and_29_out, and_30_out, and_31_out, and_32_out,
       and_33_out, and_34_out, and_35_out, and_36_out, and_37_out, and_38_out, and_39_out, and_40_out,
       and_41_out, and_42_out, and_43_out, and_44_out, and_45_out, and_46_out, and_47_out, and_48_out,
       and_49_out, and_50_out, and_51_out, and_52_out, and_53_out, and_54_out, and_55_out, and_56_out,
       and_57_out, and_58_out, and_59_out, and_60_out, and_61_out, and_62_out, and_63_out, and_64_out,
       and_65_out, and_66_out, and_67_out, and_68_out, and_69_out, and_70_out, and_71_out, and_72_out,
       and_73_out, and_76_out, and_77_out, and_78_out, and_79_out, and_80_out, and_81_out, and_82_out,
       and_83_out, and_84_out, and_85_out, and_86_out, and_87_out, and_88_out, and_89_out, and_90_out,
       and_91_out, and_92_out, and_93_out, and_94_out, and_95_out, and_96_out, and_97_out, and_98_out,
       and_99_out, and_100_out, and_101_out, and_102_out, and_103_out, and_104_out, and_105_out, and_106_out,
       and_107_out, and_108_out, and_109_out, and_110_out, and_111_out, and_112_out, and_113_out,
       and_114_out, and_115_out, and_116_out, and_117_out, and_118_out, and_119_out, and_120_out,
       and_121_out, and_122_out, and_123_out, and_124_out, and_125_out, and_126_out, and_127_out,
       and_128_out, B1, b1_t, B2, b2_t, C1, c1_t, C2, c2_t, D2, d2_t, E2, e2_t, F2, f2_t, G2, g2_t,
       not_1_out, not_2_out, not_3_out, not_4_out, not_5_out, not_6_out, not_7_out, not_8_out, not_9_out,
       not_10_out;
  wire [2:0] multiplexer_1_out, multiplexer_3_out;
  wire [3:0] multiplexer_2_out, multiplexer_4_out;

  not not_1 (not_1_out, in_1[4]);
  not not_2 (not_2_out, in_1[3]);
  not not_3 (not_3_out, in_1[2]);
  not not_4 (not_4_out, in_1[1]);
  not not_5 (not_5_out, in_1[0]);
  and and_1 (and_1_out, not_5_out, not_2_out, in_1[4]);
  and and_2 (and_2_out, in_1[1], in_1[3], not_1_out);
  and and_3 (and_3_out, not_4_out, not_2_out, in_1[4]);
  and and_4 (and_4_out, in_1[2], in_1[3], not_1_out);
  and and_5 (and_5_out, not_3_out, not_2_out, in_1[4]);
  and and_6 (and_6_out, not_5_out, not_2_out, in_1[4]);
  and and_7 (and_7_out, in_1[1], in_1[3], not_1_out);
  and and_8 (and_8_out, not_4_out, not_2_out, in_1[4]);
  and and_9 (and_9_out, in_1[2], in_1[3], not_1_out);
  and and_10 (and_10_out, not_3_out, not_2_out, in_1[4]);
  and and_11 (and_11_out, not_5_out, not_4_out, not_2_out, in_1[4]);
  and and_12 (and_12_out, not_5_out, in_1[1], in_1[3], in_1[4]);
  and and_13 (and_13_out, not_5_out, not_4_out, not_3_out);
  and and_14 (and_14_out, in_1[0], in_1[1], not_2_out);
  and and_15 (and_15_out, in_1[0], not_4_out, in_1[3]);
  and and_16 (and_16_out, not_5_out, not_3_out, not_1_out);
  and and_17 (and_17_out, in_1[0], in_1[2], not_1_out);
  and and_18 (and_18_out, in_1[0], not_3_out, in_1[4]);
  and and_19 (and_19_out, in_1[1], in_1[2], not_2_out);
  and and_20 (and_20_out, not_4_out, in_1[3], not_1_out);
  and and_21 (and_21_out, not_5_out, not_4_out, in_1[2]);
  and and_22 (and_22_out, in_1[0], in_1[1], not_2_out);
  and and_23 (and_23_out, not_5_out, in_1[2], in_1[3]);
  and and_24 (and_24_out, in_1[1], not_3_out, not_2_out);
  and and_25 (and_25_out, not_4_out, in_1[3]);
  and and_26 (and_26_out, not_3_out, not_1_out);
  and and_27 (and_27_out, in_1[2], in_1[4]);
  and and_28 (and_28_out, in_1[1], in_1[2], not_1_out);
  and and_29 (and_29_out, not_4_out, not_2_out, not_1_out);
  and and_30 (and_30_out, in_1[1], not_2_out, in_1[4]);
  and and_31 (and_31_out, not_4_out, in_1[3], in_1[4]);
  and and_32 (and_32_out, not_4_out, not_3_out);
  and and_33 (and_33_out, not_3_out, in_1[3]);
  and and_34 (and_34_out, in_1[0], in_1[1], not_3_out, not_2_out);
  and and_35 (and_35_out, in_1[0], not_4_out, in_1[2], in_1[3]);
  and and_36 (and_36_out, in_1[0], not_4_out, in_1[2], not_1_out);
  and and_37 (and_37_out, in_1[0], in_1[1], not_3_out, in_1[4]);
  and and_38 (and_38_out, not_5_out, in_1[1], in_1[2], in_1[4]);
  and and_39 (and_39_out, not_5_out, in_1[1], not_2_out, not_1_out);
  and and_40 (and_40_out, not_5_out, not_4_out, in_1[3], not_1_out);
  and and_41 (and_41_out, not_5_out, not_4_out, not_2_out, in_1[4]);
  and and_42 (and_42_out, in_1[0], in_1[2], in_1[3], not_1_out);
  and and_43 (and_43_out, in_1[0], not_3_out, not_2_out, in_1[4]);
  and and_44 (and_44_out, not_5_out, not_4_out, not_3_out);
  and and_45 (and_45_out, not_5_out, not_3_out, in_1[3]);
  and and_46 (and_46_out, not_5_out, in_1[1], in_1[2], in_1[4]);
  and and_47 (and_47_out, not_5_out, in_1[1], not_2_out, not_1_out);
  and and_48 (and_48_out, not_5_out, not_4_out, in_1[3], not_1_out);
  and and_49 (and_49_out, not_5_out, not_4_out, not_2_out, in_1[4]);
  and and_50 (and_50_out, not_5_out, not_4_out, not_3_out);
  and and_51 (and_51_out, not_5_out, not_3_out, in_1[3]);
  and and_52 (and_52_out, not_5_out, in_1[1], in_1[2], not_2_out);
  and and_53 (and_53_out, not_5_out, not_4_out, not_2_out, not_1_out);
  and and_54 (and_54_out, not_5_out, in_1[1], in_1[3], not_1_out);
  and and_55 (and_55_out, not_5_out, in_1[1], not_2_out, in_1[4]);
  and and_56 (and_56_out, not_5_out, not_4_out, in_1[3], in_1[4]);
  and and_57 (and_57_out, not_4_out, in_1[2], not_2_out, not_1_out);
  and and_58 (and_58_out, not_4_out, not_3_out, in_1[3], not_1_out);
  and and_59 (and_59_out, in_1[1], in_1[2], in_1[3], not_1_out);
  and and_60 (and_60_out, not_4_out, not_3_out, not_2_out, in_1[4]);
  and and_61 (and_61_out, in_1[1], in_1[2], not_2_out, in_1[4]);
  and and_62 (and_62_out, in_1[1], not_3_out, in_1[3], in_1[4]);
  and and_63 (and_63_out, not_5_out, in_1[1], not_2_out, not_1_out);
  and and_64 (and_64_out, in_1[0], in_1[1], not_2_out, in_1[4]);
  and and_65 (and_65_out, not_5_out, not_4_out, in_1[4]);
  and and_66 (and_66_out, not_5_out, in_1[3], in_1[4]);
  and and_67 (and_67_out, in_1[1], not_3_out, not_2_out);
  and and_68 (and_68_out, not_4_out, in_1[2], in_1[3]);
  and and_69 (and_69_out, not_4_out, in_1[2], not_1_out);
  and and_70 (and_70_out, in_1[1], not_3_out, in_1[4]);
  and and_71 (and_71_out, not_4_out, in_1[3], not_1_out);
  and and_72 (and_72_out, in_1[2], in_1[3], not_1_out);
  and and_73 (and_73_out, not_3_out, not_2_out, in_1[4]);
  or or_1 (b1_t, and_1_out, and_2_out, and_3_out, and_4_out, and_5_out);
  or or_2 (c1_t, and_6_out, and_7_out, and_8_out, and_9_out, and_10_out);
  or or_3 (a2_t, and_11_out, and_12_out, and_13_out, and_14_out, and_15_out, and_16_out, and_17_out, and_18_out, and_19_out, and_20_out);
  or or_4 (b2_t, and_21_out, and_22_out, and_23_out, and_24_out, and_25_out, and_26_out, and_27_out);
  or or_5 (c2_t, in_1[0], and_28_out, and_29_out, and_30_out, and_31_out, and_32_out, and_33_out);
  or or_6 (e2_t, and_46_out, and_47_out, and_48_out, and_49_out, and_50_out, and_51_out);
  or or_7 (f2_t, and_52_out, and_53_out, and_54_out, and_55_out, and_56_out, and_57_out, and_58_out, and_59_out, and_60_out, and_61_out, and_62_out);
  or or_8 (g2_t, and_63_out, and_64_out, and_65_out, and_66_out, and_67_out, and_68_out, and_69_out, and_70_out, and_71_out, and_72_out, and_73_out);
  or or_9 (d2_t, and_34_out, and_35_out, and_36_out, and_37_out, and_38_out, and_39_out, and_40_out, and_41_out, and_42_out, and_43_out, and_44_out, and_45_out);
  not not_6 (not_6_out, in_1[4]);
  not not_7 (not_7_out, in_1[3]);
  not not_8 (not_8_out, in_1[2]);
  not not_9 (not_9_out, in_1[1]);
  not not_10 (not_10_out, in_1[0]);
  and and_74 (B1, not_10_out, not_9_out, not_8_out, not_7_out, in_1[4]);
  and and_75 (C1, not_10_out, not_9_out, not_8_out, not_7_out, in_1[4]);
  and and_76 (and_76_out, in_1[0], not_9_out, in_1[3]);
  and and_77 (and_77_out, in_1[0], in_1[2], not_7_out);
  and and_78 (and_78_out, not_10_out, in_1[1]);
  and and_79 (and_79_out, not_10_out, not_8_out);
  and and_80 (and_80_out, in_1[1], not_8_out);
  and and_81 (and_81_out, in_1[3], not_6_out);
  and and_82 (and_82_out, not_7_out, in_1[4]);
  and and_83 (and_83_out, not_10_out, not_9_out, not_7_out, not_6_out);
  and and_84 (and_84_out, not_10_out, not_9_out, not_8_out);
  and and_85 (and_85_out, in_1[0], in_1[1], not_7_out);
  and and_86 (and_86_out, in_1[0], not_9_out, in_1[3]);
  and and_87 (and_87_out, in_1[0], in_1[2], in_1[4]);
  and and_88 (and_88_out, in_1[1], in_1[2], in_1[4]);
  and and_89 (and_89_out, not_9_out, in_1[3], in_1[4]);
  and and_90 (and_90_out, not_8_out, not_6_out);
  and and_91 (and_91_out, not_10_out, not_9_out, not_8_out);
  and and_92 (and_92_out, in_1[0], in_1[1], not_8_out);
  and and_93 (and_93_out, in_1[0], not_9_out, in_1[2]);
  and and_94 (and_94_out, in_1[0], in_1[1], in_1[4]);
  and and_95 (and_95_out, in_1[1], in_1[2], not_7_out);
  and and_96 (and_96_out, not_9_out, not_7_out, not_6_out);
  and and_97 (and_97_out, not_9_out, in_1[3], in_1[4]);
  and and_98 (and_98_out, not_8_out, in_1[3]);
  and and_99 (and_99_out, not_10_out, in_1[1], in_1[2], not_6_out);
  and and_100 (and_100_out, not_10_out, not_9_out, in_1[3], not_6_out);
  and and_101 (and_101_out, not_10_out, not_9_out, not_7_out, in_1[4]);
  and and_102 (and_102_out, not_10_out, in_1[1], in_1[3], in_1[4]);
  and and_103 (and_103_out, not_10_out, not_9_out, not_8_out);
  and and_104 (and_104_out, in_1[0], in_1[1], not_8_out);
  and and_105 (and_105_out, in_1[0], not_9_out, in_1[2]);
  and and_106 (and_106_out, not_10_out, not_8_out, not_7_out);
  and and_107 (and_107_out, not_10_out, in_1[1]);
  and and_108 (and_108_out, not_10_out, not_8_out);
  and and_109 (and_109_out, in_1[1], in_1[3], not_6_out);
  and and_110 (and_110_out, not_9_out, not_7_out, in_1[4]);
  and and_111 (and_111_out, in_1[2], in_1[3], not_6_out);
  and and_112 (and_112_out, not_8_out, not_7_out, in_1[4]);
  and and_113 (and_113_out, not_10_out, in_1[2], not_7_out);
  and and_114 (and_114_out, not_10_out, not_9_out);
  and and_115 (and_115_out, not_9_out, in_1[2], not_7_out);
  and and_116 (and_116_out, in_1[1], not_8_out, in_1[3]);
  and and_117 (and_117_out, in_1[3], not_6_out);
  and and_118 (and_118_out, not_7_out, in_1[4]);
  and and_119 (and_119_out, in_1[0], not_9_out, not_7_out, in_1[4]);
  and and_120 (and_120_out, in_1[0], in_1[2], not_7_out, in_1[4]);
  and and_121 (and_121_out, not_10_out, in_1[3], in_1[4]);
  and and_122 (and_122_out, not_10_out, in_1[1]);
  and and_123 (and_123_out, not_9_out, in_1[2], not_7_out, not_6_out);
  and and_124 (and_124_out, not_9_out, in_1[2], in_1[3], in_1[4]);
  and and_125 (and_125_out, in_1[1], not_8_out, in_1[3]);
  and and_126 (and_126_out, in_1[1], not_8_out, not_6_out);
  and and_127 (and_127_out, in_1[1], in_1[3], not_6_out);
  and and_128 (and_128_out, not_8_out, in_1[3], not_6_out);
  or or_10 (A2, and_76_out, and_77_out, and_78_out, and_79_out, and_80_out, and_81_out, and_82_out);
  or or_11 (E2, and_107_out, and_108_out, and_109_out, and_110_out, and_111_out, and_112_out);
  or or_12 (F2, and_113_out, and_114_out, and_115_out, and_116_out, and_117_out, and_118_out);
  or or_13 (B2, and_83_out, and_84_out, and_85_out, and_86_out, and_87_out, and_88_out, and_89_out, and_90_out);
  or or_14 (C2, and_91_out, and_92_out, and_93_out, and_94_out, and_95_out, and_96_out, and_97_out, and_98_out);
  or or_15 (D2, and_99_out, and_100_out, and_101_out, and_102_out, and_103_out, and_104_out, and_105_out, and_106_out);
  or or_16 (G2, and_119_out, and_120_out, and_121_out, and_122_out, and_123_out, and_124_out, and_125_out, and_126_out, and_127_out, and_128_out);
  Seven_Seg seven_seg_1 (.a(1'b0), .b(1'b0), .c(1'b0), .d(1'b0), .e(1'b0), .f(1'b0), .g(in_1[4]), .dp(1'b0));
  Seven_Seg seven_seg_2 (.a(1'b0), .b(1'b0), .c(1'b0), .d(1'b0), .e(1'b0), .f(1'b0), .g(in_1[4]), .dp(1'b0));
  Seven_Seg seven_seg_3 (.a(1'b0), .b(B1), .c(C1), .d(1'b0), .e(1'b0), .f(1'b0), .g(1'b0), .dp(1'b1));
  Seven_Seg seven_seg_4 (.a(1'b0), .b(b1_t), .c(c1_t), .d(1'b0), .e(1'b0), .f(1'b0), .g(1'b0), .dp(1'b1));
  Seven_Seg seven_seg_5 (.a(A2), .b(B2), .c(C2), .d(D2), .e(E2), .f(F2), .g(G2), .dp(1'b1));
  Seven_Seg seven_seg_6 (.a(a2_t), .b(b2_t), .c(c2_t), .d(d2_t), .e(e2_t), .f(f2_t), .g(g2_t), .dp(1'b1));
  Seven_Seg seven_seg_7 (.a(1'b0), .b(1'b0), .c(1'b0), .d(1'b0), .e(1'b0), .f(1'b0), .g(in_1[4]), .dp(1'b0));
  Seven_Seg seven_seg_8 (
    .a(multiplexer_2_out[3]), .b(multiplexer_2_out[2]), .c(multiplexer_2_out[1]), .d(multiplexer_2_out[0]),
    .e(multiplexer_1_out[0]), .f(multiplexer_1_out[1]), .g(multiplexer_1_out[2]), .dp(1'b1));
  Multiplexer #(.Bits(3)) multiplexer_1 (.sel(HEX), .in_0(3'b000), .in_1(3'b000), .out(multiplexer_1_out));
  Multiplexer #(.Bits(4)) multiplexer_2 (
    .sel(HEX), .in_0({1'b0, B1, C1, 1'b0}), .in_1({1'b0, b1_t, c1_t, 1'b0}), .out(multiplexer_2_out));
  Seven_Seg seven_seg_9 (
    .a(multiplexer_4_out[3]), .b(multiplexer_4_out[2]), .c(multiplexer_4_out[1]), .d(multiplexer_4_out[0]),
    .e(multiplexer_3_out[0]), .f(multiplexer_3_out[1]), .g(multiplexer_3_out[2]), .dp(1'b1));
  Multiplexer #(.Bits(3)) multiplexer_3 (
    .sel(HEX), .in_0({G2, F2, E2}), .in_1({g2_t, f2_t, e2_t}), .out(multiplexer_3_out));
  Multiplexer #(.Bits(4)) multiplexer_4 (
    .sel(HEX), .in_0({A2, B2, C2, D2}), .in_1({a2_t, b2_t, c2_t, d2_t}), .out(multiplexer_4_out));

  // Other names for the same wires on the sheet: By0 = in_1[0]; By1 = in_1[1]; By2 = in_1[2]; By3 = in_1[3];
  //   By4 = in_1[4]
endmodule
