// Digital circuit Representación numeros con signo en display.dig as structural Verilog
module \Representación_numeros_con_signo_en_display  (
  input  [4:0] Num,
  output a1,
  output b1,
  output c1,
  output d1,
  output e1,
  output f1,
  output g1,
  output a2,
  output b2,
  output c2,
  output d2,
  output e2,
  output f2,
  output g2
);

  wire and_1_out, and_2_out, and_3_out, and_4_out, and_5_out, and_6_out, and_7_out, and_8_out, and_9_out,
       and_10_out, and_11_out, and_12_out, and_13_out, and_14_out, and_15_out, and_16_out, and_17_out,
       and_18_out, and_19_out, and_20_out, and_21_out, and_22_out, and_23_out, and_24_out, and_25_out,
       and_26_out, and_27_out, and_28_out, and_29_out, and_30_out, and_31_out, and_32_out, and_33_out,
       and_34_out, and_35_out, and_36_out, and_37_out, and_38_out, and_39_out, and_40_out, and_41_out,
       and_42_out, and_43_out, and_44_out, and_45_out, and_46_out, and_47_out, and_48_out, and_49_out,
       and_50_out, and_51_out, and_52_out, and_53_out, and_54_out, and_55_out, and_56_out, and_57_out,
       and_58_out, and_59_out, and_60_out, and_61_out, and_62_out, and_63_out, and_64_out, and_65_out,
       and_66_out, and_67_out, and_68_out, not_1_out, not_2_out, not_3_out, not_4_out, not_5_out, not_6_out;

  Seven_Seg #(.commonCathode("true"), .commonConnectionType("anode")) seven_seg_1 (
    .a(1'b1), .b(1'b1), .c(1'b1), .d(1'b1), .e(1'b1), .f(1'b1), .g(not_1_out), .dp(1'b1), .common(1'b1));
  not not_1 (not_1_out, Num[4]);
  Seven_Seg #(.commonCathode("true"), .commonConnectionType("anode")) seven_seg_2 (
    .a(a1), .b(1'b0), .c(1'b0), .d(d1), .e(e1), .f(f1), .g(1'b1), .dp(1'b1), .common(1'b1));
  Seven_Seg #(.commonCathode("true"), .commonConnectionType("anode")) seven_seg_3 (
    .a(a2), .b(b2), .c(c2), .d(d2), .e(e2), .f(f2), .g(g2), .dp(1'b1), .common(1'b1));
  not not_2 (not_2_out, Num[4]);
  not not_3 (not_3_out, Num[3]);
  not not_4 (not_4_out, Num[2]);
  not not_5 (not_5_out, Num[1]);
  not not_6 (not_6_out, Num[0]);
  and and_1 (and_1_out, not_6_out, not_3_out, Num[4]);
  and and_2 (and_2_out, Num[1], Num[3], not_2_out);
  and and_3 (and_3_out, not_5_out, not_3_out, Num[4]);
  and and_4 (and_4_out, Num[2], Num[3], not_2_out);
  and and_5 (and_5_out, not_4_out, not_3_out, Num[4]);
  and and_6 (and_6_out, not_6_out, not_3_out, Num[4]);
  and and_7 (and_7_out, Num[1], Num[3], not_2_out);
  and and_8 (and_8_out, not_5_out, not_3_out, Num[4]);
  and and_9 (and_9_out, Num[2], Num[3], not_2_out);
  and and_10 (and_10_out, not_4_out, not_3_out, Num[4]);
  and and_11 (and_11_out, not_6_out, not_3_out, Num[4]);
  and and_12 (and_12_out, Num[1], Num[3], not_2_out);
  and and_13 (and_13_out, not_5_out, not_3_out, Num[4]);
  and and_14 (and_14_out, Num[2], Num[3], not_2_out);
  and and_15 (and_15_out, not_4_out, not_3_out, Num[4]);
  and and_16 (and_16_out, not_6_out, not_3_out, Num[4]);
  and and_17 (and_17_out, Num[1], Num[3], not_2_out);
  and and_18 (and_18_out, not_5_out, not_3_out, Num[4]);
  and and_19 (and_19_out, Num[2], Num[3], not_2_out);
  and and_20 (and_20_out, not_4_out, not_3_out, Num[4]);
  and and_21 (and_21_out, Num[0], not_5_out, not_4_out, not_3_out, not_2_out);
  and and_22 (and_22_out, Num[0], Num[1], not_4_out, Num[3], not_2_out);
  and and_23 (and_23_out, Num[0], not_5_out, Num[2], not_3_out, Num[4]);
  and and_24 (and_24_out, not_6_out, not_5_out, Num[2], Num[3], Num[4]);
  and and_25 (and_25_out, Num[0], Num[1], Num[2], Num[3], Num[4]);
  and and_26 (and_26_out, not_6_out, Num[1], Num[2], not_2_out);
  and and_27 (and_27_out, not_6_out, Num[1], not_4_out, Num[4]);
  and and_28 (and_28_out, not_6_out, Num[2], not_3_out, not_2_out);
  and and_29 (and_29_out, not_6_out, not_4_out, not_3_out, Num[4]);
  and and_30 (and_30_out, Num[0], not_5_out, Num[2], not_3_out, not_2_out);
  and and_31 (and_31_out, not_6_out, Num[1], Num[2], not_3_out, not_2_out);
  and and_32 (and_32_out, Num[0], Num[1], Num[2], Num[3], not_2_out);
  and and_33 (and_33_out, not_5_out, not_4_out, not_3_out, Num[4]);
  and and_34 (and_34_out, Num[1], not_4_out, Num[3], Num[4]);
  and and_35 (and_35_out, not_6_out, Num[1], not_4_out, not_3_out, not_2_out);
  and and_36 (and_36_out, not_6_out, not_5_out, Num[2], Num[3], not_2_out);
  and and_37 (and_37_out, not_6_out, not_5_out, Num[2], not_3_out, Num[4]);
  and and_38 (and_38_out, not_6_out, Num[1], Num[2], Num[3], Num[4]);
  and and_39 (and_39_out, not_6_out, not_5_out, Num[2], not_3_out, not_2_out);
  and and_40 (and_40_out, not_6_out, Num[1], Num[2], Num[3], not_2_out);
  and and_41 (and_41_out, not_6_out, Num[1], not_4_out, not_3_out, Num[4]);
  and and_42 (and_42_out, not_6_out, not_5_out, Num[2], Num[3], Num[4]);
  and and_43 (and_43_out, Num[0], Num[1], Num[2], not_3_out);
  and and_44 (and_44_out, Num[0], not_5_out, not_4_out, Num[3]);
  and and_45 (and_45_out, Num[0], not_5_out, not_4_out, not_2_out);
  and and_46 (and_46_out, Num[0], Num[1], Num[2], Num[4]);
  and and_47 (and_47_out, Num[0], not_4_out, Num[3], not_2_out);
  and and_48 (and_48_out, Num[0], Num[2], not_3_out, Num[4]);
  and and_49 (and_49_out, not_5_out, Num[2], not_3_out, not_2_out);
  and and_50 (and_50_out, Num[1], Num[2], Num[3], not_2_out);
  and and_51 (and_51_out, Num[1], not_4_out, not_3_out, Num[4]);
  and and_52 (and_52_out, not_5_out, Num[2], Num[3], Num[4]);
  and and_53 (and_53_out, Num[0], Num[1], not_4_out, not_3_out);
  and and_54 (and_54_out, Num[0], Num[1], not_4_out, not_2_out);
  and and_55 (and_55_out, Num[0], Num[1], not_3_out, not_2_out);
  and and_56 (and_56_out, Num[0], not_5_out, Num[3], Num[4]);
  and and_57 (and_57_out, Num[0], not_4_out, not_3_out, not_2_out);
  and and_58 (and_58_out, Num[1], not_4_out, not_3_out, not_2_out);
  and and_59 (and_59_out, not_5_out, Num[2], Num[3], not_2_out);
  and and_60 (and_60_out, not_5_out, Num[2], not_3_out, Num[4]);
  and and_61 (and_61_out, Num[1], Num[2], Num[3], Num[4]);
  and and_62 (and_62_out, Num[0], Num[1], Num[2], not_3_out, not_2_out);
  and and_63 (and_63_out, Num[0], not_5_out, Num[2], not_3_out, Num[4]);
  and and_64 (and_64_out, not_6_out, Num[1], Num[2], not_3_out, Num[4]);
  and and_65 (and_65_out, Num[0], not_5_out, not_4_out, Num[3], Num[4]);
  and and_66 (and_66_out, Num[0], Num[1], Num[2], Num[3], Num[4]);
  and and_67 (and_67_out, not_5_out, not_4_out, not_3_out, not_2_out);
  and and_68 (and_68_out, Num[1], not_4_out, Num[3], not_2_out);
  or or_1 (a1, and_1_out, and_2_out, and_3_out, and_4_out, and_5_out);
  or or_2 (d1, and_6_out, and_7_out, and_8_out, and_9_out, and_10_out);
  or or_3 (e1, and_11_out, and_12_out, and_13_out, and_14_out, and_15_out);
  or or_4 (f1, and_16_out, and_17_out, and_18_out, and_19_out, and_20_out);
  or or_5 (a2, and_21_out, and_22_out, and_23_out, and_24_out, and_25_out, and_26_out, and_27_out, and_28_out, and_29_out);
  or or_6 (b2, and_30_out, and_31_out, and_32_out, and_33_out, and_34_out);
  or or_7 (c2, and_35_out, and_36_out, and_37_out, and_38_out);
  or or_8 (d2, and_39_out, and_40_out, and_41_out, and_42_out, and_43_out, and_44_out, and_45_out, and_46_out, and_47_out, and_48_out);
  or or_9 (e2, Num[0], and_49_out, and_50_out, and_51_out, and_52_out);
  or or_10 (f2, and_53_out, and_54_out, and_55_out, and_56_out, and_57_out, and_58_out, and_59_out, and_60_out, and_61_out);
  or or_11 (g2, and_62_out, and_63_out, and_64_out, and_65_out, and_66_out, and_67_out, and_68_out);

  assign b1 = 1'b0;
  assign c1 = 1'b0;
  assign g1 = 1'b1;

  // Other names for the same wires on the sheet: msb = Num[4]
endmodule
