// Digital circuit circuito bcd(1).dig as structural Verilog
module circuito_bcd_1 (
  input  [3:0] in_1
);

  wire a, a2, b, b2, c, c2, d, d2, e, e2, f, f2, g, g2;
  wire [3:0] NUMD, NUMI;

  Multiplexer #(.Bits(4), .Selector_Bits(4)) multiplexer_1 (
    .sel(in_1), .in_0(4'b0000), .in_1(4'b0001), .in_2(4'b0010), .in_3(4'b0011), .in_4(4'b0100),
    .in_5(4'b0101), .in_6(4'b0110), .in_7(4'b0111), .in_8(4'b1000), .in_9(4'b1001), .in_10(4'b0000),
    .in_11(4'b0001), .in_12(4'b0010), .in_13(4'b0011), .in_14(4'b0100), .in_15(4'b0101), .out(NUMD));
  _7447 _7447_1 (
    .pin1(NUMI[1]), .pin2(NUMI[2]), .pin3(1'b1), .pin4(1'b1), .pin5(1'b1), .pin6(NUMI[3]), .pin7(NUMI[0]),
    .pin8(1'b0), .pin9(e2), .pin10(d2), .pin11(c2), .pin12(b2), .pin13(a2), .pin14(g2), .pin15(f2),
    .pin16(1'b1));
  _7447 _7447_2 (
    .pin1(NUMD[1]), .pin2(NUMD[2]), .pin3(1'b1), .pin4(1'b1), .pin5(1'b1), .pin6(NUMD[3]), .pin7(NUMD[0]),
    .pin8(1'b0), .pin9(e), .pin10(d), .pin11(c), .pin12(b), .pin13(a), .pin14(g), .pin15(f), .pin16(1'b1));
  Multiplexer #(.Selector_Bits(4), .Bits(4)) multiplexer_2 (
    .sel(in_1), .in_0(4'b0000), .in_1(4'b0000), .in_2(4'b0000), .in_3(4'b0000), .in_4(4'b0000),
    .in_5(4'b0000), .in_6(4'b0000), .in_7(4'b0000), .in_8(4'b0000), .in_9(4'b0000), .in_10(4'b0001),
    .in_11(4'b0001), .in_12(4'b0001), .in_13(4'b0001), .in_14(4'b0001), .in_15(4'b0001), .out(NUMI));
  Seven_Seg #(.commonCathode("true"), .commonConnectionType("anode")) seven_seg_1 (
    .a(a2), .b(b2), .c(c2), .d(d2), .e(e2), .f(f2), .g(g2), .dp(1'b1), .common(1'b1));
  Seven_Seg #(.commonConnectionType("anode"), .commonCathode("true")) seven_seg_2 (
    .a(a), .b(b), .c(c), .d(d), .e(e), .f(f), .g(g), .dp(1'b1), .common(1'b1));

  // Other names for the same wires on the sheet: NUM[3:0] = in_1
endmodule
