// Digital circuit circuito bcd.dig as structural Verilog
module circuito_bcd (
  input  [3:0] in_1
);

  wire a, b, c, d, e, f, g;

  _7447 _7447_1 (
    .pin1(in_1[1]), .pin2(in_1[2]), .pin3(1'b1), .pin4(1'b1), .pin5(1'b1), .pin6(in_1[3]), .pin7(in_1[0]),
    .pin8(1'b0), .pin9(e), .pin10(d), .pin11(c), .pin12(b), .pin13(a), .pin14(g), .pin15(f), .pin16(1'b1));
  Seven_Seg #(.commonConnectionType("anode"), .commonCathode("true")) seven_seg_1 (
    .a(a), .b(b), .c(c), .d(d), .e(e), .f(f), .g(g), .dp(1'b1), .common(1'b1));

  // Other names for the same wires on the sheet: NUM[3:0] = in_1
endmodule
