// Digital circuit MultiplicacionConCompuertasLogicas.dig as structural Verilog
module MultiplicacionConCompuertasLogicas (
  input  [3:0] in_1,
  input  [3:0] in_2,
  output [5:0] out_3
);

  wire and_5_out, and_7_out, and_9_out, and_11_out, and_14_out, and_15_out, and_16_out, and_17_out,
       and_18_out, and_19_out, and_20_out, and_21_out, or_1_out, or_2_out, xor_2_out, xor_4_out, xor_7_out;

  // And and_1 has open pins: In_1=in_1[3], In_2=in_2[3], out=open
  // And and_2 has open pins: In_1=in_1[3], In_2=in_2[2], out=open
  // And and_3 has open pins: In_1=in_1[3], In_2=in_2[1], out=open
  // And and_4 has open pins: In_1=in_1[3], In_2=in_2[0], out=open
  and and_5 (and_5_out, in_1[1], in_2[3]);
  // And and_6 has open pins: In_1=in_1[2], In_2=in_2[3], out=open
  and and_7 (and_7_out, in_1[1], in_2[2]);
  // And and_8 has open pins: In_1=in_1[2], In_2=in_2[2], out=open
  and and_9 (and_9_out, in_1[1], in_2[1]);
  // And and_10 has open pins: In_1=in_1[2], In_2=in_2[1], out=open
  and and_11 (and_11_out, in_1[1], in_2[0]);
  // And and_12 has open pins: In_1=in_1[2], In_2=in_2[0], out=open
  and and_13 (out_3[5], or_1_out, and_5_out);
  LED led_1 (.in(out_3[5]));
  and and_14 (and_14_out, and_16_out, and_7_out);
  xor xor_1 (out_3[4], or_1_out, and_5_out);
  LED led_2 (.in(out_3[4]));
  xor xor_2 (xor_2_out, and_16_out, and_7_out);
  and and_15 (and_15_out, or_2_out, xor_2_out);
  or or_1 (or_1_out, and_15_out, and_14_out);
  and and_16 (and_16_out, in_1[0], in_2[3]);
  and and_17 (and_17_out, and_19_out, and_9_out);
  xor xor_3 (out_3[3], or_2_out, xor_2_out);
  LED led_3 (.in(out_3[3]));
  xor xor_4 (xor_4_out, and_19_out, and_9_out);
  and and_18 (and_18_out, and_20_out, xor_4_out);
  or or_2 (or_2_out, and_18_out, and_17_out);
  and and_19 (and_19_out, in_1[0], in_2[2]);
  and and_20 (and_20_out, and_11_out, and_21_out);
  xor xor_5 (out_3[2], and_20_out, xor_4_out);
  LED led_4 (.in(out_3[2]));
  xor xor_6 (out_3[1], and_21_out, and_11_out);
  LED led_5 (.in(out_3[1]));
  and and_21 (and_21_out, in_1[0], in_2[1]);
  and and_22 (out_3[0], in_1[0], in_2[0]);
  LED led_6 (.in(out_3[0]));
  xor xor_7 (xor_7_out, in_1[3], in_2[3]);
  LED B0 (.in(xor_7_out));
  LED B1 (.in(xor_7_out));
  LED B2 (.in(xor_7_out));
  LED B3 (.in(xor_7_out));
  LED B4 (.in(xor_7_out));
  LED B5 (.in(xor_7_out));
  LED B6 (.in(xor_7_out));
  LED B7 (.in(xor_7_out));

  // Other names for the same wires on the sheet: b0 = in_1[0]; b1 = in_1[1]; b2 = in_1[2]; b3 = in_1[3]; b4 = in_2[0];
  //   b5 = in_2[1]; b6 = in_2[2]; b7 = in_2[3]

  // Notes on the sheet:
  //   CAJA NEGRA CA2
endmodule
