// Digital circuit PruebaNum2.dig as structural Verilog
module PruebaNum2 (
  input  A,
  input  B,
  input  C,
  input  D,
  input  E,
  output [2:0] out_6
);

  wire and_2_out, and_3_out, and_4_out, and_5_out, and_6_out, and_7_out, and_8_out, and_9_out, not_1_out,
       not_2_out, not_3_out, not_4_out;

  not not_1 (not_1_out, A);
  not not_2 (not_2_out, B);
  not not_3 (not_3_out, C);
  not not_4 (not_4_out, D);
  and and_1 (out_6[2], not_1_out, B, C);
  and and_2 (and_2_out, not_1_out, not_2_out, C, D);
  and and_3 (and_3_out, not_1_out, B, not_3_out);
  and and_4 (and_4_out, not_1_out, not_3_out, D, E);
  and and_5 (and_5_out, not_1_out, not_2_out, C, not_4_out);
  and and_6 (and_6_out, A, B);
  and and_7 (and_7_out, B, D, E);
  and and_8 (and_8_out, B, not_3_out, E);
  and and_9 (and_9_out, B, not_3_out, D);
  or or_1 (out_6[1], and_2_out, and_3_out);
  or or_2 (out_6[0], and_4_out, and_5_out, and_6_out, and_7_out, and_8_out, and_9_out);
endmodule
