// Digital circuit ExamenCarlo.dig as structural Verilog
module ExamenCarlo (
  input  [7:0] n1,
  input  [7:0] n2,
  input  [7:0] n3,
  input  [7:0] n4,
  input  [7:0] n5,
  input  [7:0] n6,
  input  [7:0] n7,
  input  [7:0] n8,
  input  [7:0] n9,
  input  [7:0] n10,
  input  [4:0] comparador,
  output [7:0] out_12,
  output [7:0] out_13,
  output [7:0] out_14,
  output [7:0] out_15,
  output [11:0] out_16,
  output [7:0] out_17,
  output [7:0] out_18,
  output [7:0] out_19,
  output [7:0] out_20,
  output [11:0] out_21,
  output [11:0] out_22,
  output [7:0] out_23,
  output [7:0] out_24,
  output [7:0] out_25,
  output [7:0] out_26,
  output [11:0] out_27,
  output [7:0] out_28,
  output [7:0] out_29,
  output [7:0] out_30,
  output [7:0] out_31,
  output [11:0] out_32,
  output [11:0] out_33,
  output [7:0] out_34,
  output [7:0] out_35,
  output [7:0] out_36,
  output [7:0] out_37,
  output [11:0] out_38,
  output [7:0] out_39,
  output [7:0] out_40,
  output [7:0] out_41,
  output [7:0] out_42,
  output [11:0] out_43,
  output [11:0] out_44,
  output [7:0] out_45,
  output [7:0] out_46,
  output [7:0] out_47,
  output [7:0] out_48,
  output [11:0] out_49,
  output [7:0] out_50,
  output [7:0] out_51,
  output [7:0] out_52,
  output [7:0] out_53,
  output [11:0] out_54,
  output [11:0] out_55,
  output [7:0] out_56,
  output [7:0] out_57,
  output [7:0] out_58,
  output [7:0] out_59,
  output [11:0] out_60,
  output [7:0] out_61,
  output [7:0] out_62,
  output [7:0] out_63,
  output [7:0] out_64,
  output [11:0] out_65,
  output [11:0] out_66,
  output [7:0] out_67,
  output [7:0] out_68,
  output [7:0] out_69,
  output [7:0] out_70,
  output [11:0] out_71,
  output [7:0] out_72,
  output [7:0] out_73,
  output [7:0] out_74,
  output [7:0] out_75,
  output [11:0] out_76,
  output [11:0] out_77,
  output [7:0] out_78,
  output [7:0] out_79,
  output [7:0] out_80,
  output [7:0] out_81,
  output [11:0] out_82,
  output [7:0] out_83,
  output [7:0] out_84,
  output [7:0] out_85,
  output [7:0] out_86,
  output [11:0] out_87,
  output [11:0] out_88,
  output [7:0] out_89,
  output [7:0] out_90,
  output [7:0] out_91,
  output [7:0] out_92,
  output [11:0] out_93,
  output [7:0] out_94,
  output [7:0] out_95,
  output [7:0] out_96,
  output [7:0] out_97,
  output [11:0] out_98,
  output [11:0] out_99,
  output [7:0] out_100,
  output [7:0] out_101,
  output [7:0] out_102,
  output [7:0] out_103,
  output [11:0] out_104,
  output [7:0] out_105,
  output [7:0] out_106,
  output [7:0] out_107,
  output [7:0] out_108,
  output [11:0] out_109,
  output [11:0] out_110,
  output [7:0] out_111,
  output [7:0] out_112,
  output [7:0] out_113,
  output [7:0] out_114,
  output [11:0] out_115,
  output [7:0] out_116,
  output [7:0] out_117,
  output [7:0] out_118,
  output [7:0] out_119,
  output [11:0] out_120,
  output [11:0] out_121,
  output [11:0] out_122,
  output [11:0] out_123,
  output [11:0] out_124,
  output [11:0] out_125,
  output [3:0] out_126,
  output [11:0] out_127,
  output [11:0] out_128,
  output [11:0] out_129,
  output [11:0] out_130,
  output [3:0] out_131,
  output [11:0] out_132,
  output [11:0] out_133
);

  wire comparator_1_gt, comparator_2_eq, comparator_3_gt, comparator_4_eq, comparator_5_gt, comparator_6_eq,
       comparator_7_gt, comparator_8_eq, comparator_9_gt, comparator_10_eq, comparator_11_gt,
       comparator_12_eq, comparator_13_gt, comparator_14_eq, comparator_15_gt, comparator_16_eq,
       comparator_17_gt, comparator_18_eq, comparator_19_gt, comparator_20_eq, comparator_21_gt,
       comparator_22_eq, comparator_23_gt, comparator_24_eq, comparator_25_gt, comparator_26_eq,
       comparator_27_gt, comparator_28_eq, comparator_29_gt, comparator_30_eq, comparator_31_gt,
       comparator_32_eq, comparator_33_gt, comparator_34_eq, comparator_35_gt, comparator_36_eq,
       comparator_37_gt, comparator_38_eq, comparator_39_gt, comparator_40_eq;
  wire [0:0] ContNeg1, ContNeg2, ContNeg3, ContNeg4, ContNeg5, ContNeg6, ContNeg7, ContNeg8, ContNeg9,
       ContNeg10, ContPos1, ContPos2, ContPos3, ContPos4, ContPos5, ContPos6, ContPos7, ContPos8, ContPos9,
       ContPos10;
  wire [3:0] add_8_s, add_9_s, add_10_s, add_11_s, add_12_s, add_13_s, add_16_s, add_18_s, add_26_s,
       add_27_s, add_28_s, add_29_s, add_30_s, add_31_s, add_32_s, add_36_s;
  wire [7:0] multiplexer_1_out, multiplexer_2_out, multiplexer_3_out, multiplexer_4_out, multiplexer_5_out,
       multiplexer_6_out, multiplexer_7_out, multiplexer_8_out, multiplexer_9_out, multiplexer_10_out,
       multiplexer_21_out, multiplexer_22_out, multiplexer_23_out, multiplexer_24_out, multiplexer_25_out,
       multiplexer_26_out, multiplexer_27_out, multiplexer_28_out, multiplexer_29_out, multiplexer_30_out;

  Neg #(.Bits(8)) neg_1 (.in(n1), .out(out_14));
  Neg #(.Bits(8)) neg_2 (.in(n2), .out(out_19));
  Neg #(.Bits(8)) neg_3 (.in(n3), .out(out_36));
  Neg #(.Bits(8)) neg_4 (.in(n4), .out(out_41));
  Neg #(.Bits(8)) neg_5 (.in(n5), .out(out_91));
  Neg #(.Bits(8)) neg_6 (.in(n6), .out(out_96));
  Neg #(.Bits(8)) neg_7 (.in(n7), .out(out_102));
  Neg #(.Bits(8)) neg_8 (.in(n8), .out(out_107));
  Neg #(.Bits(8)) neg_9 (.in(n9), .out(out_113));
  Neg #(.Bits(8)) neg_10 (.in(n10), .out(out_118));
  Multiplexer #(.Bits(8)) multiplexer_1 (.sel(n1[7]), .in_0(n1), .in_1({8{1'b0}}), .out(multiplexer_1_out));
  Multiplexer #(.Bits(8)) multiplexer_2 (.sel(n2[7]), .in_0(n2), .in_1({8{1'b0}}), .out(multiplexer_2_out));
  Multiplexer #(.Bits(8)) multiplexer_3 (.sel(n3[7]), .in_0(n3), .in_1({8{1'b0}}), .out(multiplexer_3_out));
  Multiplexer #(.Bits(8)) multiplexer_4 (.sel(n4[7]), .in_0(n4), .in_1({8{1'b0}}), .out(multiplexer_4_out));
  Multiplexer #(.Bits(8)) multiplexer_5 (.sel(n5[7]), .in_0(n5), .in_1({8{1'b0}}), .out(multiplexer_5_out));
  Multiplexer #(.Bits(8)) multiplexer_6 (.sel(n6[7]), .in_0(n6), .in_1({8{1'b0}}), .out(multiplexer_6_out));
  Multiplexer #(.Bits(8)) multiplexer_7 (.sel(n7[7]), .in_0(n7), .in_1({8{1'b0}}), .out(multiplexer_7_out));
  Multiplexer #(.Bits(8)) multiplexer_8 (.sel(n8[7]), .in_0(n8), .in_1({8{1'b0}}), .out(multiplexer_8_out));
  Multiplexer #(.Bits(8)) multiplexer_9 (.sel(n9[7]), .in_0(n9), .in_1({8{1'b0}}), .out(multiplexer_9_out));
  Multiplexer #(.Bits(8)) multiplexer_10 (.sel(n10[7]), .in_0(n10), .in_1({8{1'b0}}), .out(multiplexer_10_out));
  Div #(.Bits(8)) div_1 (.a(multiplexer_1_out), .b({3'b000, comparador}), .q(out_12), .r(out_13));
  Div #(.Bits(8)) div_2 (.a(multiplexer_2_out), .b({3'b000, comparador}), .q(out_17), .r(out_18));
  Div #(.Bits(8)) div_3 (.a(multiplexer_3_out), .b({3'b000, comparador}), .q(out_34), .r(out_35));
  Div #(.Bits(8)) div_4 (.a(multiplexer_4_out), .b({3'b000, comparador}), .q(out_39), .r(out_40));
  Div #(.Bits(8)) div_5 (.a(multiplexer_5_out), .b({3'b000, comparador}), .q(out_89), .r(out_90));
  Div #(.Bits(8)) div_6 (.a(multiplexer_6_out), .b({3'b000, comparador}), .q(out_94), .r(out_95));
  Div #(.Bits(8)) div_7 (.a(multiplexer_7_out), .b({3'b000, comparador}), .q(out_100), .r(out_101));
  Div #(.Bits(8)) div_8 (.a(multiplexer_8_out), .b({3'b000, comparador}), .q(out_105), .r(out_106));
  Div #(.Bits(8)) div_9 (.a(multiplexer_9_out), .b({3'b000, comparador}), .q(out_111), .r(out_112));
  Div #(.Bits(8)) div_10 (.a(multiplexer_10_out), .b({3'b000, comparador}), .q(out_116), .r(out_117));
  Comparator #(.Bits(8)) comparator_1 (.a(out_12), .b({8{1'b0}}), .gt(comparator_1_gt));  // open: eq, lt
  Comparator #(.Bits(8)) comparator_2 (.a(out_13), .b({8{1'b0}}), .eq(comparator_2_eq));  // open: gt, lt
  Comparator #(.Bits(8)) comparator_3 (.a(out_17), .b({8{1'b0}}), .gt(comparator_3_gt));  // open: eq, lt
  Comparator #(.Bits(8)) comparator_4 (.a(out_18), .b({8{1'b0}}), .eq(comparator_4_eq));  // open: gt, lt
  Comparator #(.Bits(8)) comparator_5 (.a(out_34), .b({8{1'b0}}), .gt(comparator_5_gt));  // open: eq, lt
  Comparator #(.Bits(8)) comparator_6 (.a(out_35), .b({8{1'b0}}), .eq(comparator_6_eq));  // open: gt, lt
  Comparator #(.Bits(8)) comparator_7 (.a(out_39), .b({8{1'b0}}), .gt(comparator_7_gt));  // open: eq, lt
  Comparator #(.Bits(8)) comparator_8 (.a(out_40), .b({8{1'b0}}), .eq(comparator_8_eq));  // open: gt, lt
  Comparator #(.Bits(8)) comparator_9 (.a(out_89), .b({8{1'b0}}), .gt(comparator_9_gt));  // open: eq, lt
  Comparator #(.Bits(8)) comparator_10 (.a(out_90), .b({8{1'b0}}), .eq(comparator_10_eq));  // open: gt, lt
  Comparator #(.Bits(8)) comparator_11 (.a(out_94), .b({8{1'b0}}), .gt(comparator_11_gt));  // open: eq, lt
  Comparator #(.Bits(8)) comparator_12 (.a(out_95), .b({8{1'b0}}), .eq(comparator_12_eq));  // open: gt, lt
  Comparator #(.Bits(8)) comparator_13 (.a(out_100), .b({8{1'b0}}), .gt(comparator_13_gt));  // open: eq, lt
  Comparator #(.Bits(8)) comparator_14 (.a(out_101), .b({8{1'b0}}), .eq(comparator_14_eq));  // open: gt, lt
  Comparator #(.Bits(8)) comparator_15 (.a(out_105), .b({8{1'b0}}), .gt(comparator_15_gt));  // open: eq, lt
  Comparator #(.Bits(8)) comparator_16 (.a(out_106), .b({8{1'b0}}), .eq(comparator_16_eq));  // open: gt, lt
  Comparator #(.Bits(8)) comparator_17 (.a(out_111), .b({8{1'b0}}), .gt(comparator_17_gt));  // open: eq, lt
  Comparator #(.Bits(8)) comparator_18 (.a(out_112), .b({8{1'b0}}), .eq(comparator_18_eq));  // open: gt, lt
  Comparator #(.Bits(8)) comparator_19 (.a(out_116), .b({8{1'b0}}), .gt(comparator_19_gt));  // open: eq, lt
  Comparator #(.Bits(8)) comparator_20 (.a(out_117), .b({8{1'b0}}), .eq(comparator_20_eq));  // open: gt, lt
  and and_1 (ContPos1[0], comparator_1_gt, comparator_2_eq);
  and and_2 (ContPos2[0], comparator_3_gt, comparator_4_eq);
  and and_3 (ContPos3[0], comparator_5_gt, comparator_6_eq);
  and and_4 (ContPos4[0], comparator_7_gt, comparator_8_eq);
  and and_5 (ContPos5[0], comparator_9_gt, comparator_10_eq);
  and and_6 (ContPos6[0], comparator_11_gt, comparator_12_eq);
  and and_7 (ContPos7[0], comparator_13_gt, comparator_14_eq);
  and and_8 (ContPos8[0], comparator_15_gt, comparator_16_eq);
  and and_9 (ContPos9[0], comparator_17_gt, comparator_18_eq);
  and and_10 (ContPos10[0], comparator_19_gt, comparator_20_eq);
  Multiplexer #(.Bits(8)) multiplexer_11 (.sel(ContPos1[0]), .in_0({8{1'b0}}), .in_1(n1), .out(out_15));
  Multiplexer #(.Bits(8)) multiplexer_12 (.sel(ContPos2[0]), .in_0({8{1'b0}}), .in_1(n2), .out(out_20));
  Multiplexer #(.Bits(8)) multiplexer_13 (.sel(ContPos3[0]), .in_0({8{1'b0}}), .in_1(n3), .out(out_37));
  Multiplexer #(.Bits(8)) multiplexer_14 (.sel(ContPos4[0]), .in_0({8{1'b0}}), .in_1(n4), .out(out_42));
  Multiplexer #(.Bits(8)) multiplexer_15 (.sel(ContPos5[0]), .in_0({8{1'b0}}), .in_1(n5), .out(out_92));
  Multiplexer #(.Bits(8)) multiplexer_16 (.sel(ContPos6[0]), .in_0({8{1'b0}}), .in_1(n6), .out(out_97));
  Multiplexer #(.Bits(8)) multiplexer_17 (.sel(ContPos7[0]), .in_0({8{1'b0}}), .in_1(n7), .out(out_103));
  Multiplexer #(.Bits(8)) multiplexer_18 (.sel(ContPos8[0]), .in_0({8{1'b0}}), .in_1(n8), .out(out_108));
  Multiplexer #(.Bits(8)) multiplexer_19 (.sel(ContPos9[0]), .in_0({8{1'b0}}), .in_1(n9), .out(out_114));
  Multiplexer #(.Bits(8)) multiplexer_20 (.sel(ContPos10[0]), .in_0({8{1'b0}}), .in_1(n10), .out(out_119));
  Add #(.Bits(12)) add_1 (.a({4'b0000, out_15}), .b({4'b0000, out_20}), .c_i(1'b0), .s(out_22));  // open: c_o
  Add #(.Bits(12)) add_2 (.a({4'b0000, out_37}), .b({4'b0000, out_42}), .c_i(1'b0), .s(out_44));  // open: c_o
  Add #(.Bits(12)) add_3 (.a({4'b0000, out_92}), .b({4'b0000, out_97}), .c_i(1'b0), .s(out_99));  // open: c_o
  Add #(.Bits(12)) add_4 (.a({4'b0000, out_103}), .b({4'b0000, out_108}), .c_i(1'b0), .s(out_110));  // open: c_o
  Add #(.Bits(12)) add_5 (.a({4'b0000, out_114}), .b({4'b0000, out_119}), .c_i(1'b0), .s(out_121));  // open: c_o
  Add #(.Bits(12)) add_6 (.a(out_22), .b(out_44), .c_i(1'b0), .s(out_122));  // open: c_o
  Add #(.Bits(12)) add_7 (.a(out_122), .b(out_99), .c_i(1'b0), .s(out_123));  // open: c_o
  Add #(.Bits(4)) add_8 (.a({3'b000, ContPos3[0]}), .b({3'b000, ContPos4[0]}), .c_i(1'b0), .s(add_8_s));  // open: c_o
  Add #(.Bits(4)) add_9 (.a({3'b000, ContPos7[0]}), .b({3'b000, ContPos8[0]}), .c_i(1'b0), .s(add_9_s));  // open: c_o
  Add #(.Bits(4)) add_10 (.a({3'b000, ContPos1[0]}), .b({3'b000, ContPos2[0]}), .c_i(1'b0), .s(add_10_s));  // open: c_o
  Add #(.Bits(4)) add_11 (.a({3'b000, ContPos5[0]}), .b({3'b000, ContPos6[0]}), .c_i(1'b0), .s(add_11_s));  // open: c_o
  Add #(.Bits(4)) add_12 (
    .a({3'b000, ContPos9[0]}), .b({3'b000, ContPos10[0]}), .c_i(1'b0), .s(add_12_s));  // open: c_o
  Add #(.Bits(4)) add_13 (.a(add_10_s), .b(add_8_s), .c_i(1'b0), .s(add_13_s));  // open: c_o
  Add #(.Bits(12)) add_14 (.a(out_123), .b(out_110), .c_i(1'b0), .s(out_124));  // open: c_o
  Add #(.Bits(12)) add_15 (.a(out_124), .b(out_121), .c_i(1'b0), .s(out_125));  // open: c_o
  Add #(.Bits(4)) add_16 (.a(add_11_s), .b(add_9_s), .c_i(1'b0), .s(add_16_s));  // open: c_o
  Add #(.Bits(4)) add_17 (.a(add_18_s), .b(add_12_s), .c_i(1'b0), .s(out_126));  // open: c_o
  Div #(.Bits(12)) div_11 (.a(out_125), .b({{8{1'b0}}, out_126}), .q(out_132));  // open: r
  Add #(.Bits(4)) add_18 (.a(add_13_s), .b(add_16_s), .c_i(1'b0), .s(add_18_s));  // open: c_o
  Neg #(.Bits(8)) neg_11 (.in(n1), .out(out_25));
  Neg #(.Bits(8)) neg_12 (.in(n2), .out(out_30));
  Neg #(.Bits(8)) neg_13 (.in(n3), .out(out_47));
  Neg #(.Bits(8)) neg_14 (.in(n4), .out(out_52));
  Neg #(.Bits(8)) neg_15 (.in(n5), .out(out_58));
  Neg #(.Bits(8)) neg_16 (.in(n6), .out(out_63));
  Neg #(.Bits(8)) neg_17 (.in(n7), .out(out_69));
  Neg #(.Bits(8)) neg_18 (.in(n8), .out(out_74));
  Neg #(.Bits(8)) neg_19 (.in(n9), .out(out_80));
  Neg #(.Bits(8)) neg_20 (.in(n10), .out(out_85));
  Multiplexer #(.Bits(8)) multiplexer_21 (.sel(n1[7]), .in_0({8{1'b0}}), .in_1(out_25), .out(multiplexer_21_out));
  Multiplexer #(.Bits(8)) multiplexer_22 (.sel(n2[7]), .in_0({8{1'b0}}), .in_1(out_30), .out(multiplexer_22_out));
  Multiplexer #(.Bits(8)) multiplexer_23 (.sel(n3[7]), .in_0({8{1'b0}}), .in_1(out_47), .out(multiplexer_23_out));
  Multiplexer #(.Bits(8)) multiplexer_24 (.sel(n4[7]), .in_0({8{1'b0}}), .in_1(out_52), .out(multiplexer_24_out));
  Multiplexer #(.Bits(8)) multiplexer_25 (.sel(n5[7]), .in_0({8{1'b0}}), .in_1(out_58), .out(multiplexer_25_out));
  Multiplexer #(.Bits(8)) multiplexer_26 (.sel(n6[7]), .in_0({8{1'b0}}), .in_1(out_63), .out(multiplexer_26_out));
  Multiplexer #(.Bits(8)) multiplexer_27 (.sel(n7[7]), .in_0({8{1'b0}}), .in_1(out_69), .out(multiplexer_27_out));
  Multiplexer #(.Bits(8)) multiplexer_28 (.sel(n8[7]), .in_0({8{1'b0}}), .in_1(out_74), .out(multiplexer_28_out));
  Multiplexer #(.Bits(8)) multiplexer_29 (.sel(n9[7]), .in_0({8{1'b0}}), .in_1(out_80), .out(multiplexer_29_out));
  Multiplexer #(.Bits(8)) multiplexer_30 (.sel(n10[7]), .in_0({8{1'b0}}), .in_1(out_85), .out(multiplexer_30_out));
  Div #(.Bits(8)) div_12 (.a(multiplexer_21_out), .b({3'b000, comparador}), .q(out_23), .r(out_24));
  Div #(.Bits(8)) div_13 (.a(multiplexer_22_out), .b({3'b000, comparador}), .q(out_28), .r(out_29));
  Div #(.Bits(8)) div_14 (.a(multiplexer_23_out), .b({3'b000, comparador}), .q(out_45), .r(out_46));
  Div #(.Bits(8)) div_15 (.a(multiplexer_24_out), .b({3'b000, comparador}), .q(out_50), .r(out_51));
  Div #(.Bits(8)) div_16 (.a(multiplexer_25_out), .b({3'b000, comparador}), .q(out_56), .r(out_57));
  Div #(.Bits(8)) div_17 (.a(multiplexer_26_out), .b({3'b000, comparador}), .q(out_61), .r(out_62));
  Div #(.Bits(8)) div_18 (.a(multiplexer_27_out), .b({3'b000, comparador}), .q(out_67), .r(out_68));
  Div #(.Bits(8)) div_19 (.a(multiplexer_28_out), .b({3'b000, comparador}), .q(out_72), .r(out_73));
  Div #(.Bits(8)) div_20 (.a(multiplexer_29_out), .b({3'b000, comparador}), .q(out_78), .r(out_79));
  Div #(.Bits(8)) div_21 (.a(multiplexer_30_out), .b({3'b000, comparador}), .q(out_83), .r(out_84));
  Comparator #(.Bits(8)) comparator_21 (.a(out_23), .b({8{1'b0}}), .gt(comparator_21_gt));  // open: eq, lt
  Comparator #(.Bits(8)) comparator_22 (.a(out_24), .b({8{1'b0}}), .eq(comparator_22_eq));  // open: gt, lt
  Comparator #(.Bits(8)) comparator_23 (.a(out_28), .b({8{1'b0}}), .gt(comparator_23_gt));  // open: eq, lt
  Comparator #(.Bits(8)) comparator_24 (.a(out_29), .b({8{1'b0}}), .eq(comparator_24_eq));  // open: gt, lt
  Comparator #(.Bits(8)) comparator_25 (.a(out_45), .b({8{1'b0}}), .gt(comparator_25_gt));  // open: eq, lt
  Comparator #(.Bits(8)) comparator_26 (.a(out_46), .b({8{1'b0}}), .eq(comparator_26_eq));  // open: gt, lt
  Comparator #(.Bits(8)) comparator_27 (.a(out_50), .b({8{1'b0}}), .gt(comparator_27_gt));  // open: eq, lt
  Comparator #(.Bits(8)) comparator_28 (.a(out_51), .b({8{1'b0}}), .eq(comparator_28_eq));  // open: gt, lt
  Comparator #(.Bits(8)) comparator_29 (.a(out_56), .b({8{1'b0}}), .gt(comparator_29_gt));  // open: eq, lt
  Comparator #(.Bits(8)) comparator_30 (.a(out_57), .b({8{1'b0}}), .eq(comparator_30_eq));  // open: gt, lt
  Comparator #(.Bits(8)) comparator_31 (.a(out_61), .b({8{1'b0}}), .gt(comparator_31_gt));  // open: eq, lt
  Comparator #(.Bits(8)) comparator_32 (.a(out_62), .b({8{1'b0}}), .eq(comparator_32_eq));  // open: gt, lt
  Comparator #(.Bits(8)) comparator_33 (.a(out_67), .b({8{1'b0}}), .gt(comparator_33_gt));  // open: eq, lt
  Comparator #(.Bits(8)) comparator_34 (.a(out_68), .b({8{1'b0}}), .eq(comparator_34_eq));  // open: gt, lt
  Comparator #(.Bits(8)) comparator_35 (.a(out_72), .b({8{1'b0}}), .gt(comparator_35_gt));  // open: eq, lt
  Comparator #(.Bits(8)) comparator_36 (.a(out_73), .b({8{1'b0}}), .eq(comparator_36_eq));  // open: gt, lt
  Comparator #(.Bits(8)) comparator_37 (.a(out_78), .b({8{1'b0}}), .gt(comparator_37_gt));  // open: eq, lt
  Comparator #(.Bits(8)) comparator_38 (.a(out_79), .b({8{1'b0}}), .eq(comparator_38_eq));  // open: gt, lt
  Comparator #(.Bits(8)) comparator_39 (.a(out_83), .b({8{1'b0}}), .gt(comparator_39_gt));  // open: eq, lt
  Comparator #(.Bits(8)) comparator_40 (.a(out_84), .b({8{1'b0}}), .eq(comparator_40_eq));  // open: gt, lt
  and and_11 (ContNeg1[0], comparator_21_gt, comparator_22_eq);
  and and_12 (ContNeg2[0], comparator_23_gt, comparator_24_eq);
  and and_13 (ContNeg3[0], comparator_25_gt, comparator_26_eq);
  and and_14 (ContNeg4[0], comparator_27_gt, comparator_28_eq);
  and and_15 (ContNeg5[0], comparator_29_gt, comparator_30_eq);
  and and_16 (ContNeg6[0], comparator_31_gt, comparator_32_eq);
  and and_17 (ContNeg7[0], comparator_33_gt, comparator_34_eq);
  and and_18 (ContNeg8[0], comparator_35_gt, comparator_36_eq);
  and and_19 (ContNeg9[0], comparator_37_gt, comparator_38_eq);
  and and_20 (ContNeg10[0], comparator_39_gt, comparator_40_eq);
  Multiplexer #(.Bits(8)) multiplexer_31 (.sel(ContNeg1[0]), .in_0({8{1'b0}}), .in_1(out_25), .out(out_26));
  Multiplexer #(.Bits(8)) multiplexer_32 (.sel(ContNeg2[0]), .in_0({8{1'b0}}), .in_1(out_30), .out(out_31));
  Multiplexer #(.Bits(8)) multiplexer_33 (.sel(ContNeg3[0]), .in_0({8{1'b0}}), .in_1(out_47), .out(out_48));
  Multiplexer #(.Bits(8)) multiplexer_34 (.sel(ContNeg4[0]), .in_0({8{1'b0}}), .in_1(out_52), .out(out_53));
  Multiplexer #(.Bits(8)) multiplexer_35 (.sel(ContNeg5[0]), .in_0({8{1'b0}}), .in_1(out_58), .out(out_59));
  Multiplexer #(.Bits(8)) multiplexer_36 (.sel(ContNeg6[0]), .in_0({8{1'b0}}), .in_1(out_63), .out(out_64));
  Multiplexer #(.Bits(8)) multiplexer_37 (.sel(ContNeg7[0]), .in_0({8{1'b0}}), .in_1(out_69), .out(out_70));
  Multiplexer #(.Bits(8)) multiplexer_38 (.sel(ContNeg8[0]), .in_0({8{1'b0}}), .in_1(out_74), .out(out_75));
  Multiplexer #(.Bits(8)) multiplexer_39 (.sel(ContNeg9[0]), .in_0({8{1'b0}}), .in_1(out_80), .out(out_81));
  Multiplexer #(.Bits(8)) multiplexer_40 (.sel(ContNeg10[0]), .in_0({8{1'b0}}), .in_1(out_85), .out(out_86));
  Add #(.Bits(12)) add_19 (.a({4'b0000, out_26}), .b({4'b0000, out_31}), .c_i(1'b0), .s(out_33));  // open: c_o
  Add #(.Bits(12)) add_20 (.a({4'b0000, out_48}), .b({4'b0000, out_53}), .c_i(1'b0), .s(out_55));  // open: c_o
  Add #(.Bits(12)) add_21 (.a({4'b0000, out_59}), .b({4'b0000, out_64}), .c_i(1'b0), .s(out_66));  // open: c_o
  Add #(.Bits(12)) add_22 (.a({4'b0000, out_70}), .b({4'b0000, out_75}), .c_i(1'b0), .s(out_77));  // open: c_o
  Add #(.Bits(12)) add_23 (.a({4'b0000, out_81}), .b({4'b0000, out_86}), .c_i(1'b0), .s(out_88));  // open: c_o
  Add #(.Bits(12)) add_24 (.a(out_33), .b(out_55), .c_i(1'b0), .s(out_127));  // open: c_o
  Add #(.Bits(12)) add_25 (.a(out_127), .b(out_66), .c_i(1'b0), .s(out_128));  // open: c_o
  Add #(.Bits(4)) add_26 (.a({3'b000, ContNeg3[0]}), .b({3'b000, ContNeg4[0]}), .c_i(1'b0), .s(add_26_s));  // open: c_o
  Add #(.Bits(4)) add_27 (.a({3'b000, ContNeg7[0]}), .b({3'b000, ContNeg8[0]}), .c_i(1'b0), .s(add_27_s));  // open: c_o
  Add #(.Bits(4)) add_28 (.a({3'b000, ContNeg1[0]}), .b({3'b000, ContNeg2[0]}), .c_i(1'b0), .s(add_28_s));  // open: c_o
  Add #(.Bits(4)) add_29 (.a({3'b000, ContNeg5[0]}), .b({3'b000, ContNeg6[0]}), .c_i(1'b0), .s(add_29_s));  // open: c_o
  Add #(.Bits(4)) add_30 (
    .a({3'b000, ContNeg9[0]}), .b({3'b000, ContNeg10[0]}), .c_i(1'b0), .s(add_30_s));  // open: c_o
  Add #(.Bits(4)) add_31 (.a(add_28_s), .b(add_26_s), .c_i(1'b0), .s(add_31_s));  // open: c_o
  Add #(.Bits(4)) add_32 (.a(add_29_s), .b(add_27_s), .c_i(1'b0), .s(add_32_s));  // open: c_o
  Add #(.Bits(12)) add_33 (.a(out_128), .b(out_77), .c_i(1'b0), .s(out_129));  // open: c_o
  Add #(.Bits(12)) add_34 (.a(out_129), .b(out_88), .c_i(1'b0), .s(out_130));  // open: c_o
  Add #(.Bits(4)) add_35 (.a(add_36_s), .b(add_30_s), .c_i(1'b0), .s(out_131));  // open: c_o
  Div #(.Bits(12)) div_22 (.a(out_130), .b({{8{1'b0}}, out_131}), .q(out_133));  // open: r
  Add #(.Bits(4)) add_36 (.a(add_31_s), .b(add_32_s), .c_i(1'b0), .s(add_36_s));  // open: c_o

  assign out_16 = {4'b0000, out_15};
  assign out_21 = {4'b0000, out_20};
  assign out_27 = {4'b0000, out_26};
  assign out_32 = {4'b0000, out_31};
  assign out_38 = {4'b0000, out_37};
  assign out_43 = {4'b0000, out_42};
  assign out_49 = {4'b0000, out_48};
  assign out_54 = {4'b0000, out_53};
  assign out_60 = {4'b0000, out_59};
  assign out_65 = {4'b0000, out_64};
  assign out_71 = {4'b0000, out_70};
  assign out_76 = {4'b0000, out_75};
  assign out_82 = {4'b0000, out_81};
  assign out_87 = {4'b0000, out_86};
  assign out_93 = {4'b0000, out_92};
  assign out_98 = {4'b0000, out_97};
  assign out_104 = {4'b0000, out_103};
  assign out_109 = {4'b0000, out_108};
  assign out_115 = {4'b0000, out_114};
  assign out_120 = {4'b0000, out_119};

  // Other names for the same wires on the sheet: comp8bit[4:0] = comparador; TOTALPOSITIVOS[3:0] = out_126;
  //   TOTALNEGATIVOS[3:0] = out_131; SUMNEGATIVOS[11:0] = out_130; SUMPOSITIVOS[11:0] = out_125

  // Notes on the sheet:
  //   POSITIVOS
  //   SUMATORIA TOTAL POSITIVOS
  //   PROMEDIO POSITIVOS
  //   TOTAL DE POSITIVOS
  //   Negativos
  //   PROMEDIO NEGATIVOS
  //   SUMATORIA TOTAL NEGATIVOS
  //   TOTAL DE NEGATIVOS
endmodule
