// Digital circuit Display7Segmentos.dig as structural Verilog
module Display7Segmentos (
  input  clk
);

  Counter #(.Bits(4)) counter_1 (.en(1'b1), .C(clk), .clr(1'b0));  // open: out, ovf
  // _7447 _7447_1: pin names not known
  Seven_Seg seven_seg_1 ();  // open: a, b, c, d, e, f, g, dp
endmodule
