// Digital circuit TC1Semana6.dig as structural Verilog
module TC1Semana6 (
  input  clk,
  output [3:0] out_2,
  output [3:0] out_3,
  output [9:0] out_4
);

  wire A, a1, A2, a2_t, A3, a3_t, and_1_out, and_2_out, and_3_out, and_6_out, B, b1, B2, b2_t, B3, b3_t, C,
       c1, C2, c2_t, C3, c3_t, clk2, clk_t, comparator_1_eq, comparator_2_eq, comparator_4_eq, cut2, cut3, D,
       d1, D2, d2_t, D3, d3_t, e1, e2, e3, en2, en3, f1, f2, f3, g1, g2, g3, g4, not_2_out, or_1_out,
       or_2_out;
  wire [4:0] multiplexer_1_out, multiplexer_2_out, neg_1_out, neg_2_out;
  wire [9:0] counter_5_out;

  Comparator #(.Bits(4)) comparator_1 (.a({D2, C2, B2, A2}), .b(4'b0000), .eq(comparator_1_eq));  // open: gt, lt
  and and_1 (and_1_out, B3, C3);
  and and_2 (and_2_out, en2, comparator_1_eq);
  or or_1 (or_1_out, cut3, and_1_out);
  xnor xnor_1 (g4, 1'b0, 1'b1);
  Counter #(.Bits(4)) counter_1 (.en(en2), .C(and_2_out), .clr(or_1_out), .out({D3, C3, B3, A3}));  // open: ovf
  _7447 _7447_1 (
    .pin1(B3), .pin2(C3), .pin3(1'b1), .pin4(1'b1), .pin5(1'b1), .pin6(D3), .pin7(A3), .pin8(1'b0),
    .pin9(e3), .pin10(d3_t), .pin11(c3_t), .pin12(b3_t), .pin13(a3_t), .pin14(g3), .pin15(f3), .pin16(1'b1));
  Seven_Seg #(.commonCathode("true"), .commonConnectionType("anode")) seven_seg_1 (
    .a(1'b1), .b(1'b1), .c(1'b1), .d(1'b1), .e(1'b1), .f(1'b1), .g(g4), .dp(1'b1), .common(1'b1));
  Comparator #(.Bits(4)) comparator_2 (.a({D, C, B, A}), .b(4'b0000), .eq(comparator_2_eq));  // open: gt, lt
  and and_3 (and_3_out, A2, D2);
  and and_4 (clk2, en2, comparator_2_eq);
  or or_2 (or_2_out, cut2, and_3_out);
  Seven_Seg #(.commonCathode("true"), .commonConnectionType("anode")) seven_seg_2 (
    .a(a3_t), .b(b3_t), .c(c3_t), .d(d3_t), .e(e3), .f(f3), .g(g3), .dp(1'b1), .common(1'b1));
  _7447 _7447_2 (
    .pin1(B2), .pin2(C2), .pin3(1'b1), .pin4(1'b1), .pin5(1'b1), .pin6(D2), .pin7(A2), .pin8(1'b0),
    .pin9(e2), .pin10(d2_t), .pin11(c2_t), .pin12(b2_t), .pin13(a2_t), .pin14(g2), .pin15(f2), .pin16(1'b1));
  Seven_Seg #(.commonCathode("true"), .commonConnectionType("anode")) seven_seg_3 (
    .a(a2_t), .b(b2_t), .c(c2_t), .d(d2_t), .e(e2), .f(f2), .g(g2), .dp(1'b1), .common(1'b1));
  Counter #(.Bits(4)) counter_2 (.en(en2), .C(clk2), .clr(or_2_out), .out({D2, C2, B2, A2}));  // open: ovf
  Seven_Seg #(.commonCathode("true"), .commonConnectionType("anode")) seven_seg_4 (
    .a(a1), .b(b1), .c(c1), .d(d1), .e(e1), .f(f1), .g(g1), .dp(1'b1), .common(1'b1));
  Counter #(.Bits(4)) counter_3 (.en(cut3), .C(clk2), .clr(1'b0), .out(out_3));  // open: ovf
  Neg #(.Bits(5)) neg_1 (.in(5'b01111), .out(neg_1_out));
  Neg #(.Bits(5)) neg_2 (.in(5'b11100), .out(neg_2_out));
  Multiplexer #(.Bits(5)) multiplexer_1 (.sel(1'b0), .in_0(5'b01111), .in_1(neg_1_out), .out(multiplexer_1_out));
  Multiplexer #(.Bits(5)) multiplexer_2 (.sel(1'b1), .in_0(5'b11100), .in_1(neg_2_out), .out(multiplexer_2_out));
  Comparator #(.Bits(4)) comparator_3 (.a(out_3), .b(4'b0100), .lt(cut3));  // open: gt, eq
  not not_1 (en3, cut3);
  not not_2 (not_2_out, comparator_4_eq);
  and and_5 (clk_t, not_2_out, clk);
  and and_6 (and_6_out, A, D);
  Counter #(.Bits(4)) counter_4 (.en(1'b1), .C(clk_t), .clr(and_6_out), .out({D, C, B, A}));  // open: ovf
  _7447 _7447_3 (
    .pin1(B), .pin2(C), .pin3(1'b1), .pin4(1'b1), .pin5(1'b1), .pin6(D), .pin7(A), .pin8(1'b0), .pin9(e1),
    .pin10(d1), .pin11(c1), .pin12(b1), .pin13(a1), .pin14(g1), .pin15(f1), .pin16(1'b1));
  Mul #(.Bits(5)) mul_1 (.a(multiplexer_1_out), .b(multiplexer_2_out), .mul(out_4));
  Counter #(.Bits(10)) counter_5 (.en(1'b1), .C(clk_t), .clr(1'b0), .out(counter_5_out));  // open: ovf
  Counter #(.Bits(4)) counter_6 (.en(cut2), .C(clk_t), .clr(1'b0), .out(out_2));  // open: ovf
  Comparator #(.Bits(10)) comparator_4 (.a(out_4), .b(counter_5_out), .eq(comparator_4_eq));  // open: gt, lt
  Comparator #(.Bits(4)) comparator_5 (.a(out_2), .b(4'b0100), .lt(cut2));  // open: gt, eq
  LED led_1 (.in(comparator_4_eq));
  not not_3 (en2, cut2);

  // Other names for the same wires on the sheet: N1[3:0] = {D, C, B, A}; N2[3:0] = {D2, C2, B2, A2};
  //   N3[3:0] = {D3, C3, B3, A3}

  // Notes on the sheet:
  //   clk: Hz: 500
endmodule
