// Digital circuit CircuitoConRegistro.dig as structural Verilog
module CircuitoConRegistro (
  input  [3:0] N1,
  input  [3:0] N2,
  input  [3:0] N3,
  input  [3:0] N4,
  input  [3:0] N5,
  input  [3:0] N6,
  input  [3:0] N7,
  input  [3:0] N8,
  input  [3:0] N9,
  input  [3:0] N10,
  input  [3:0] N11,
  input  [3:0] N12,
  input  [3:0] N13,
  input  [3:0] N14,
  input  [3:0] N15,
  input  [3:0] N16,
  input  clk,
  output [7:0] out_18
);

  wire clk_t, comparator_1_eq, en, suma;
  wire [3:0] counter_1_out, out;
  wire [7:0] add_1_s;

  Button calcular (.out(suma));
  not not_1 (en, comparator_1_eq);
  and and_1 (clk_t, clk, suma);
  Comparator #(.Bits(4)) comparator_1 (.a(counter_1_out), .b(4'b1111), .eq(comparator_1_eq));  // open: gt, lt
  Counter #(.Bits(4)) counter_1 (.en(en), .C(clk_t), .clr(1'b0), .out(counter_1_out));  // open: ovf
  Multiplexer #(.Selector_Bits(4), .Bits(4)) multiplexer_1 (
    .sel(counter_1_out), .in_0(N1), .in_1(N2), .in_2(N3), .in_3(N4), .in_4(N5), .in_5(N6), .in_6(N7),
    .in_7(N8), .in_8(N9), .in_9(N10), .in_10(N11), .in_11(N12), .in_12(N13), .in_13(N14), .in_14(N15),
    .in_15(N16), .out(out));
  Register #(.Bits(8)) register_1 (.D(add_1_s), .C(clk_t), .en(en), .Q(out_18));
  Add #(.Bits(8)) add_1 (.a({4'b0000, out}), .b(out_18), .c_i(1'b0), .s(add_1_s));  // open: c_o
endmodule
