// Digital circuit CircuitoContadorComparador.dig as structural Verilog
module CircuitoContadorComparador (
  input  clk,
  output [3:0] out_2,
  output [3:0] out_3,
  output [3:0] out_4,
  output [3:0] out_5,
  output [3:0] out_6,
  output [2:0] out_7
);

  wire and_1_out, clck, comparator_1_lt, en1, en2, en3, en4;
  wire [1:0] sub_1_s;
  wire [2:0] counter_2_out;
  wire [2:2] sub_1_s_2;
  wire [3:0] multiplexer_1_out, multiplexer_3_out, multiplexer_4_out, multiplexer_5_out, multiplexer_6_out,
       reg1, reg2, reg3, reg4;

  and and_1 (and_1_out, clk, comparator_1_lt);
  Counter #(.Bits(3)) counter_1 (.en(1'b1), .C(and_1_out), .clr(1'b0), .out(out_7));  // open: ovf
  Multiplexer #(.Selector_Bits(3), .Bits(4)) multiplexer_1 (
    .sel(out_7), .in_0(4'b0111), .in_1(4'b0110), .in_2(4'b0111), .in_3(4'b0110), .in_4(4'b0101),
    .in_5(4'b0111), .in_6(4'b0101), .in_7(4'b0001), .out(multiplexer_1_out));
  Comparator #(.Bits(3)) comparator_1 (.a(out_7), .b(3'b111), .lt(comparator_1_lt));  // open: gt, eq
  Comparator #(.Bits(4)) comparator_2 (.a(multiplexer_1_out), .b(4'b0110), .gt(clck));  // open: eq, lt
  Multiplexer #(.Bits(4)) multiplexer_2 (.sel(clck), .in_0(4'b0000), .in_1(multiplexer_1_out), .out(out_6));
  Counter #(.Bits(3)) counter_2 (.en(1'b1), .C(clck), .clr(1'b0), .out(counter_2_out));  // open: ovf
  Demultiplexer #(.Selector_Bits(2), .Bits(4)) demultiplexer_1 (
    .sel(sub_1_s), .in(out_6), .out_0(reg1), .out_1(reg2), .out_2(reg3), .out_3(reg4));
  Sub #(.Bits(3)) sub_1 (.a(counter_2_out), .b(3'b001), .c_i(1'b0), .s({sub_1_s_2[2], sub_1_s}));  // open: c_o
  Comparator #(.Bits(3)) comparator_3 (.a(counter_2_out), .b(3'b001), .eq(en1));  // open: gt, lt
  Comparator #(.Bits(3)) comparator_4 (.a(counter_2_out), .b(3'b010), .eq(en2));  // open: gt, lt
  Comparator #(.Bits(3)) comparator_5 (.a(counter_2_out), .b(3'b011), .eq(en3));  // open: gt, lt
  Comparator #(.Bits(3)) comparator_6 (.a(counter_2_out), .b(3'b100), .eq(en4));  // open: gt, lt
  Multiplexer #(.Bits(4)) multiplexer_3 (.sel(en1), .in_0(4'b0000), .in_1(reg1), .out(multiplexer_3_out));
  Multiplexer #(.Bits(4)) multiplexer_4 (.sel(en2), .in_0(4'b0000), .in_1(reg2), .out(multiplexer_4_out));
  Multiplexer #(.Bits(4)) multiplexer_5 (.sel(en3), .in_0(4'b0000), .in_1(reg3), .out(multiplexer_5_out));
  Multiplexer #(.Bits(4)) multiplexer_6 (.sel(en4), .in_0(4'b0000), .in_1(reg4), .out(multiplexer_6_out));
  Register #(.Bits(4)) register_1 (.D(multiplexer_3_out), .C(clck), .en(en1), .Q(out_2));
  Register #(.Bits(4)) register_2 (.D(multiplexer_4_out), .C(clck), .en(en2), .Q(out_3));
  Register #(.Bits(4)) register_3 (.D(multiplexer_5_out), .C(clck), .en(en3), .Q(out_4));
  Register #(.Bits(4)) register_4 (.D(multiplexer_6_out), .C(clck), .en(en4), .Q(out_5));

  // Other names for the same wires on the sheet: position[2:0] = out_7
endmodule
