// Digital circuit EjercicioEnClase.dig as structural Verilog
module EjercicioEnClase (
  input  clk,
  output [63:0] out_2,
  output [31:0] out_3
);

  wire clock, comparator_1_eq, comparator_2_eq, en, not_2_out;
  wire [3:0] counter_1_out;
  wire [31:0] mul_2_mul, multiplexer_1_out;
  wire [63:32] mul_2_mul_2;

  Mul #(.Bits(32)) mul_1 (.a(32'h1fa0), .b(32'h1fa0), .mul(out_2));
  not not_1 (en, comparator_1_eq);
  Comparator #(.Bits(4)) comparator_1 (.a(counter_1_out), .b(4'b1011), .eq(comparator_1_eq));  // open: gt, lt
  Counter #(.Bits(4)) counter_1 (.en(en), .C(clk), .clr(1'b0), .out(counter_1_out));  // open: ovf
  not not_2 (not_2_out, comparator_1_eq);
  and and_1 (clock, clk, not_2_out);
  Register #(.Bits(32)) register_1 (.D(mul_2_mul), .C(clock), .en(en), .Q(out_3));
  Multiplexer #(.Bits(32)) multiplexer_1 (.sel(comparator_2_eq), .in_0(out_3), .in_1(32'h1), .out(multiplexer_1_out));
  Comparator #(.Bits(32)) comparator_2 (.a({32{1'b0}}), .b(out_3), .eq(comparator_2_eq));  // open: gt, lt
  Mul #(.Bits(32)) mul_2 (.a(32'h7), .b(multiplexer_1_out), .mul({mul_2_mul_2, mul_2_mul}));

  // Notes on the sheet:
  //   Base
  //   Potencia
endmodule
