// Digital circuit Laboratorio7.dig as structural Verilog
module Laboratorio7 (
  input  clk,
  input  in_5,
  output Da,
  output Db,
  output Dc,
  output [2:0] out_6
);

  wire and_1_out, and_2_out, and_3_out, and_4_out, and_5_out, and_6_out, and_7_out, not_1_out, not_2_out,
       not_3_out, not_4_out;

  not not_1 (not_1_out, out_6[2]);
  not not_2 (not_2_out, out_6[1]);
  not not_3 (not_3_out, out_6[0]);
  not not_4 (not_4_out, in_5);
  and and_1 (and_1_out, not_1_out, out_6[1], out_6[0]);
  and and_2 (and_2_out, out_6[2], not_2_out, not_4_out);
  and and_3 (and_3_out, not_1_out, not_2_out, out_6[0]);
  and and_4 (and_4_out, not_1_out, out_6[1], not_3_out);
  and and_5 (and_5_out, not_2_out, out_6[0], not_4_out);
  and and_6 (and_6_out, not_1_out, not_3_out);
  and and_7 (and_7_out, not_2_out, not_3_out, not_4_out);
  or or_1 (Da, and_1_out, and_2_out);
  or or_2 (Db, and_3_out, and_4_out, and_5_out);
  or or_3 (Dc, and_6_out, and_7_out);
  D_FF d_ff_1 (.D(Da), .C(clk), .Q(out_6[2]));  // open: nQ
  D_FF d_ff_2 (.D(Db), .C(clk), .Q(out_6[1]));  // open: nQ
  D_FF d_ff_3 (.D(Dc), .C(clk), .Q(out_6[0]));  // open: nQ

  // Other names for the same wires on the sheet: Clck = clk; Qa = out_6[2]; Qb = out_6[1]; Qc = out_6[0]; X = in_5
endmodule
