// Digital circuit PruebaSemana7Version3.dig as structural Verilog
module PruebaSemana7Version3 (
  input  clk,
  output [3:0] out_2,
  output [2:0] out_3,
  output Da,
  output Db,
  output Dc,
  output [3:0] out_7
);

  wire a1, a2_t, and_1_out, and_2_out, and_3_out, and_4_out, and_5_out, and_6_out, and_7_out, and_8_out,
       and_9_out, b1, b2_t, c1, c2_t, clear, comparator_2_eq, comparator_3_eq, comparator_4_eq, cut2, d1,
       d2_t, e1, e2, en2, f1, f2, g1, g2, multiplexer_1_out, not_1_out, not_2_out, not_3_out, not_4_out,
       or_4_out, or_5_out, X;
  wire [2:0] counter_1_out;

  not not_1 (not_1_out, out_3[2]);
  not not_2 (not_2_out, out_3[1]);
  not not_3 (not_3_out, out_3[0]);
  not not_4 (not_4_out, X);
  and and_1 (and_1_out, not_1_out, not_2_out, not_3_out);
  and and_2 (and_2_out, out_3[2], not_2_out, out_3[0]);
  and and_3 (and_3_out, out_3[2], out_3[0], X);
  and and_4 (and_4_out, not_1_out, not_2_out, not_3_out);
  and and_5 (and_5_out, out_3[2], not_2_out, out_3[0], X);
  and and_6 (and_6_out, out_3[2], out_3[1], out_3[0], not_4_out);
  and and_7 (and_7_out, not_1_out, not_2_out, not_3_out);
  and and_8 (and_8_out, out_3[2], out_3[0]);
  or or_1 (Da, and_1_out, and_2_out, and_3_out);
  or or_2 (Db, and_4_out, and_5_out, and_6_out);
  or or_3 (Dc, and_7_out, and_8_out);
  Multiplexer multiplexer_1 (.sel(clear), .in_0(1'b0), .in_1(clear), .out(multiplexer_1_out));
  Counter #(.Bits(3)) counter_1 (.en(1'b1), .C(clk), .clr(multiplexer_1_out), .out(counter_1_out));  // open: ovf
  Comparator #(.Bits(3)) comparator_1 (.a(counter_1_out), .b(3'b101), .eq(clear));  // open: gt, lt
  _7447 _7447_1 (
    .pin1(out_3[1]), .pin2(out_3[2]), .pin3(1'b1), .pin4(1'b1), .pin5(1'b1), .pin6(1'b0), .pin7(out_3[0]),
    .pin8(1'b0), .pin9(e2), .pin10(d2_t), .pin11(c2_t), .pin12(b2_t), .pin13(a2_t), .pin14(g2), .pin15(f2),
    .pin16(1'b1));
  and and_9 (and_9_out, out_7[0], out_7[2]);
  Seven_Seg #(.commonCathode("true"), .commonConnectionType("anode")) seven_seg_1 (
    .a(a1), .b(b1), .c(c1), .d(d1), .e(e1), .f(f1), .g(g1), .dp(1'b1), .common(1'b1));
  Counter #(.Bits(4)) counter_2 (.en(1'b1), .C(clk), .clr(and_9_out), .out(out_7));  // open: ovf
  _7447 _7447_2 (
    .pin1(out_7[1]), .pin2(out_7[2]), .pin3(1'b1), .pin4(1'b1), .pin5(1'b1), .pin6(out_7[3]),
    .pin7(out_7[0]), .pin8(1'b0), .pin9(e1), .pin10(d1), .pin11(c1), .pin12(b1), .pin13(a1), .pin14(g1),
    .pin15(f1), .pin16(1'b1));
  Seven_Seg #(.commonCathode("true"), .commonConnectionType("anode")) seven_seg_2 (
    .a(a2_t), .b(b2_t), .c(c2_t), .d(d2_t), .e(e2), .f(f2), .g(g2), .dp(1'b1), .common(1'b1));
  D_FF d_ff_1 (.D(Da), .C(clk), .Q(out_3[2]));  // open: nQ
  D_FF d_ff_2 (.D(Db), .C(clk), .Q(out_3[1]));  // open: nQ
  D_FF d_ff_3 (.D(Dc), .C(clk), .Q(out_3[0]));  // open: nQ
  Counter #(.Bits(4)) counter_3 (.en(cut2), .C(clk), .clr(1'b0), .out(out_2));  // open: ovf
  Comparator #(.Bits(4)) comparator_2 (.a(out_7), .b(4'b0000), .eq(comparator_2_eq));  // open: gt, lt
  Comparator #(.Bits(4)) comparator_3 (.a(out_7), .b(4'b0010), .eq(comparator_3_eq));  // open: gt, lt
  Comparator #(.Bits(4)) comparator_4 (.a(out_7), .b(4'b0100), .eq(comparator_4_eq));  // open: gt, lt
  Comparator #(.Bits(4)) comparator_5 (.a(out_2), .b(4'b0100), .lt(cut2));  // open: gt, eq
  not not_5 (en2, cut2);
  or or_4 (or_4_out, comparator_2_eq, comparator_3_eq);
  or or_5 (or_5_out, or_4_out, comparator_4_eq);
  not not_6 (X, or_5_out);

  // Other names for the same wires on the sheet: C2 = out_3[2]; N2[2:0] = out_3; Qa = out_3[2]; B2 = out_3[1];
  //   Qb = out_3[1]; A2 = out_3[0]; Qc = out_3[0]; A = out_7[0]; N1[3:0] = out_7; x_t[3:0] = out_7; B = out_7[1];
  //   C = out_7[2]; D = out_7[3]
endmodule
