// Digital circuit TablaCorrecta.dig as structural Verilog
module TablaCorrecta (
  input  Qa,
  input  Qb,
  input  Qc,
  input  X,
  output Da,
  output Db,
  output Dc
);

  wire and_1_out, and_2_out, and_3_out, and_4_out, and_5_out, and_6_out, and_7_out, and_8_out, not_1_out,
       not_2_out, not_3_out, not_4_out;

  not not_1 (not_1_out, Qa);
  not not_2 (not_2_out, Qb);
  not not_3 (not_3_out, Qc);
  not not_4 (not_4_out, X);
  and and_1 (and_1_out, not_1_out, not_2_out, not_3_out);
  and and_2 (and_2_out, Qa, not_2_out, Qc);
  and and_3 (and_3_out, Qa, Qc, X);
  and and_4 (and_4_out, not_1_out, not_2_out, not_3_out);
  and and_5 (and_5_out, Qa, not_2_out, Qc, X);
  and and_6 (and_6_out, Qa, Qb, Qc, not_4_out);
  and and_7 (and_7_out, not_1_out, not_2_out, not_3_out);
  and and_8 (and_8_out, Qa, Qc);
  or or_1 (Da, and_1_out, and_2_out, and_3_out);
  or or_2 (Db, and_4_out, and_5_out, and_6_out);
  or or_3 (Dc, and_7_out, and_8_out);
endmodule
