// Digital circuit TablaDePrueba.dig as structural Verilog
module TablaDePrueba (
  input  clk,
  output Da,
  output Db,
  output Dc,
  output [2:0] out_5
);

  wire and_1_out, and_2_out, and_3_out, and_4_out, and_5_out, and_6_out, and_7_out, not_1_out, not_2_out,
       not_3_out, not_4_out, t_ff_1_q, X;

  not not_1 (not_1_out, out_5[2]);
  not not_2 (not_2_out, out_5[1]);
  not not_3 (not_3_out, out_5[0]);
  not not_4 (not_4_out, X);
  and and_1 (and_1_out, not_1_out, out_5[1], out_5[0]);
  and and_2 (and_2_out, out_5[2], not_2_out, not_4_out);
  and and_3 (and_3_out, not_1_out, not_2_out, out_5[0]);
  and and_4 (and_4_out, not_1_out, out_5[1], not_3_out);
  and and_5 (and_5_out, not_2_out, out_5[0], not_4_out);
  and and_6 (and_6_out, not_1_out, not_3_out);
  and and_7 (and_7_out, not_2_out, not_3_out, not_4_out);
  or or_1 (Da, and_1_out, and_2_out);
  or or_2 (Db, and_3_out, and_4_out, and_5_out);
  or or_3 (Dc, and_6_out, and_7_out);
  T_FF t_ff_1 (.T(1'b1), .C(clk), .Q(t_ff_1_q));  // open: nQ
  D_FF d_ff_1 (.D(Da), .C(clk), .Q(out_5[2]));  // open: nQ
  D_FF d_ff_2 (.D(Db), .C(clk), .Q(out_5[1]));  // open: nQ
  D_FF d_ff_3 (.D(Dc), .C(clk), .Q(out_5[0]));  // open: nQ
  D_FF d_ff_4 (.D(t_ff_1_q), .C(clk), .Q(X));  // open: nQ

  // Other names for the same wires on the sheet: Clck = clk; Qa = out_5[2]; Qb = out_5[1]; Qc = out_5[0]
endmodule
