// Digital circuit EjercicioDeClase2.dig as structural Verilog
module EjercicioDeClase2 (
  input  [4:0] in_1,
  input  [1:0] in_2,
  input  [4:0] in_4,
  input  [4:0] in_5,
  input  [4:0] in_7,
  input  [4:0] in_8,
  input  [4:0] in_10,
  input  [4:0] in_11,
  input  [4:0] in_13,
  input  [4:0] in_14,
  input  [4:0] in_16,
  input  [1:0] in_17,
  input  [4:0] in_19,
  input  [4:0] in_21,
  output [4:0] out_3,
  output [5:0] out_6,
  output [7:0] out_9,
  output [7:0] out_12,
  output [5:0] out_15,
  output [4:0] out_18,
  output [6:0] out_20,
  output [31:0] out_22
);

  wire button_1_out, button_2_out;

  Button button_1 (.out(button_1_out));
  Button button_2 (.out(button_2_out));
  Complemento1and2 #(.applicationType("IVERILOG")) u_Complemento1and2 (.A(in_1), .op(in_2), .C1(out_3));
  Suma #(.applicationType("IVERILOG")) u_Suma (.A(in_4), .B(in_5), .C1(out_6));
  Resta #(.applicationType("IVERILOG")) u_Resta (.A(in_13), .B(in_14), .C1(out_15));
  Multiplicacion #(.applicationType("IVERILOG")) u_Multiplicacion (.A(in_7), .B(in_8), .C1(out_9));
  Division #(.applicationType("IVERILOG")) u_Division (.A(in_10), .B(in_11), .C1(out_12));
  exampleCase #(.applicationType("IVERILOG")) u_exampleCase (.A(in_16), .op(in_17), .Result(out_18));
  cicloFor #(.applicationType("IVERILOG")) u_cicloFor (.num(in_19), .calcular(button_1_out), .Result(out_20));
  factorial #(.applicationType("IVERILOG")) u_factorial (.num(in_21), .calcular(button_2_out), .Result(out_22));

  // Other names for the same wires on the sheet: c1[4:0] = out_3; c2[5:0] = out_6; c3[5:0] = out_15; c4[7:0] = out_9;
  //   c5[7:0] = out_12; c6[4:0] = out_18; c7[6:0] = out_20; c8[31:0] = out_22

  // Notes on the sheet:
  //   Normal, C1 y C2 (0,1,2)
  //   A
  //   B
endmodule

/* Code of Complemento1and2:
//segundo ejercicio
module Complemento1and2(
    input [4:0] A,
    input [1:0]op,
    output reg [4:0] C1
);

    reg[4:0] one;
    initial begin
        one=1;
    end

    always @ (*)
    begin
        
        if ( op == 0 ) // C1 es igual A
        begin
            C1 = A;
        end
        if ( op == 1)  // C1 es complemento a1 A
        begin
            C1 = ~A;
        end
        if ( op == 2)  // C1 es complemento a2 A
        begin
            C1 = (~A) + one;
        end        
    end
endmodule
*/

/* Code of Suma:
//segundo ejercicio
module Suma(
    input [4:0] A,
    input [4:0] B,
    output reg [5:0] C1
);

    reg[4:0] one;
    initial begin
        one=1;
    end

    always @ (*)
    begin
        C1 = A + B;                
    end
endmodule
*/

/* Code of Resta:
//segundo ejercicio
module Resta(
    input [4:0] A,
    input [4:0] B,
    output reg [5:0] C1
);

    reg[4:0] one;
    initial begin
        one=1;
    end

    always @ (*)
    begin
        C1 = A - B;                
    end
endmodule
*/

/* Code of Multiplicacion:
//segundo ejercicio
module Multiplicacion(
    input [4:0] A,
    input [4:0] B,
    output reg [7:0] C1
);

    reg[4:0] one;
    initial begin
        one=1;
    end

    always @ (*)
    begin
        C1 = A * B;                
    end
endmodule
*/

/* Code of Division:
//segundo ejercicio
module Division(
    input [4:0] A,
    input [4:0] B,
    output reg [7:0] C1
);

    reg[4:0] one;
    initial begin
        one=1;
    end

    always @ (*)
    begin
        C1 = A / B;                
    end
endmodule
*/

/* Code of exampleCase:
module exampleCase(
    input [4:0] A,
    input [1:0]op,
    output reg [4:0] Result
);

always @ (*)
begin
    case (op)
        1: 
            Result = A *2;
        2:
            Result = A *3;        
        default: 
            Result = A;
    endcase
end

endmodule
*/

/* Code of cicloFor:
module cicloFor(
    input [4:0] num,
    input calcular,
    output reg [6:0] Result
);

reg[4:0] i;

always @ (posedge calcular)
begin
    begin
        Result=0;
        i=0;
    end

    for (i =0 ; i<=num; i++)
    begin
        Result = Result + i ;
    end    
end

endmodule
*/

/* Code of factorial:
module factorial(
    input [4:0] num,
    input calcular,
    output reg [31:0] Result
);

reg[4:0] i;

always @ (posedge calcular)
begin
    begin
        Result=1;
        i=0;
    end

    for (i = num ; i>0; i--)
    begin
        Result = Result * i ;
    end    
end

endmodule
*/
