// Digital circuit Prueba de Verilog.dig as structural Verilog
module Prueba_de_Verilog (
  input  clk
);

  wire button_1_out, u_EJEMPLO3_x1, u_EJEMPLO3_x2;

  Button button_1 (.out(button_1_out));
  EJEMPLO3 #(.applicationType("IVERILOG")) u_EJEMPLO3 (
    .A(button_1_out), .B(clk), .C(clk), .X1(u_EJEMPLO3_x1), .X2(u_EJEMPLO3_x2));
  LED led_1 (.in(u_EJEMPLO3_x1));
  LED led_2 (.in(u_EJEMPLO3_x2));
endmodule

/* Code of EJEMPLO3:
module EJEMPLO3(
    input A,
    input B,
    input C,
    output X1,
    output X2    
);
    //wires
    wire w1;
    wire w2;
    wire w3;

    // and
    and and1 (w1, A, B);
    // xor1
    xor xor1 (w3, C, w2);
    // xor 2
    xor xor2 (X1, C, w1);
    // or;
    or or1 (X2, w1, w3);
    // not
    not not1 (w2,B);

endmodule
*/
