// Digital circuit PruebaSemana8Reloj24h.dig as structural Verilog
module PruebaSemana8Reloj24h (
  input  [4:0] in_1,
  input  [4:0] in_3,
  input  clk,
  input  in_12,
  output [31:0] out_2,
  output [6:0] out_4,
  output [1:0] out_6,
  output [3:0] out_7,
  output [3:0] out_8,
  output [3:0] out_9,
  output [3:0] out_10,
  output [3:0] out_11
);

  wire a1, a2_t, a3_t, a4_t, a5_t, a6_t, and_1_out, b1, b2_t, b3_t, b4_t, b5_t, b6_t, button_1_out,
       button_2_out, button_3_out, button_4_out, c1, c2_t, c3_t, c4_t, c5_t, C6, c6_t, d1, d2_t, d3_t, d4_t,
       d5_t, D6, d6_t, e1, e2, e3, e4, e5, e6, f1, f2, f3, f4, f5, f6, g1, g2, g3, g4, g5, g6;

  _7447 _7447_1 (
    .pin1(out_6[1]), .pin2(C6), .pin3(1'b1), .pin4(1'b1), .pin5(1'b1), .pin6(D6), .pin7(out_6[0]),
    .pin8(1'b0), .pin9(e6), .pin10(d6_t), .pin11(c6_t), .pin12(b6_t), .pin13(a6_t), .pin14(g6), .pin15(f6),
    .pin16(1'b1));
  _7447 _7447_2 (
    .pin1(out_7[1]), .pin2(out_7[2]), .pin3(1'b1), .pin4(1'b1), .pin5(1'b1), .pin6(out_7[3]),
    .pin7(out_7[0]), .pin8(1'b0), .pin9(e5), .pin10(d5_t), .pin11(c5_t), .pin12(b5_t), .pin13(a5_t),
    .pin14(g5), .pin15(f5), .pin16(1'b1));
  _7447 _7447_3 (
    .pin1(out_8[1]), .pin2(out_8[2]), .pin3(1'b1), .pin4(1'b1), .pin5(1'b1), .pin6(out_8[3]),
    .pin7(out_8[0]), .pin8(1'b0), .pin9(e4), .pin10(d4_t), .pin11(c4_t), .pin12(b4_t), .pin13(a4_t),
    .pin14(g4), .pin15(f4), .pin16(1'b1));
  Button button_1 (.out(button_1_out));
  and and_1 (and_1_out, clk, in_12);
  factorial #(.applicationType("IVERILOG")) u_factorial (.num(in_1), .calcular(button_1_out), .Result(out_2));
  Button button_2 (.out(button_2_out));
  _7447 _7447_4 (
    .pin1(out_9[1]), .pin2(out_9[2]), .pin3(1'b1), .pin4(1'b1), .pin5(1'b1), .pin6(out_9[3]),
    .pin7(out_9[0]), .pin8(1'b0), .pin9(e3), .pin10(d3_t), .pin11(c3_t), .pin12(b3_t), .pin13(a3_t),
    .pin14(g3), .pin15(f3), .pin16(1'b1));
  Button button_3 (.out(button_3_out));
  reloj24H #(.applicationType("IVERILOG")) u_reloj24H (
    .clk(and_1_out), .minutos(button_3_out), .horas(button_2_out), .segundoDer(out_11), .segundoIzq(out_10),
    .minutosDer(out_9), .minutosIzq(out_8), .horasDiDer(out_7), .horasDiIzq(out_6));
  _7447 _7447_5 (
    .pin1(out_10[1]), .pin2(out_10[2]), .pin3(1'b1), .pin4(1'b1), .pin5(1'b1), .pin6(out_10[3]),
    .pin7(out_10[0]), .pin8(1'b0), .pin9(e2), .pin10(d2_t), .pin11(c2_t), .pin12(b2_t), .pin13(a2_t),
    .pin14(g2), .pin15(f2), .pin16(1'b1));
  Button button_4 (.out(button_4_out));
  cicloFor #(.applicationType("IVERILOG")) u_cicloFor (.num(in_3), .calcular(button_4_out), .Result(out_4));
  _7447 _7447_6 (
    .pin1(out_11[1]), .pin2(out_11[2]), .pin3(1'b1), .pin4(1'b1), .pin5(1'b1), .pin6(out_11[3]),
    .pin7(out_11[0]), .pin8(1'b0), .pin9(e1), .pin10(d1), .pin11(c1), .pin12(b1), .pin13(a1), .pin14(g1),
    .pin15(f1), .pin16(1'b1));
  Seven_Seg #(.commonCathode("true"), .commonConnectionType("anode")) seven_seg_1 (
    .a(a6_t), .b(b6_t), .c(c6_t), .d(d6_t), .e(e6), .f(f6), .g(g6), .dp(1'b1), .common(1'b1));
  Seven_Seg #(.commonCathode("true"), .commonConnectionType("anode")) seven_seg_2 (
    .a(a5_t), .b(b5_t), .c(c5_t), .d(d5_t), .e(e5), .f(f5), .g(g5), .dp(1'b1), .common(1'b1));
  LED led_1 (.in(1'b1));
  LED led_2 (.in(1'b1));
  Seven_Seg #(.commonCathode("true"), .commonConnectionType("anode")) seven_seg_3 (
    .a(a4_t), .b(b4_t), .c(c4_t), .d(d4_t), .e(e4), .f(f4), .g(g4), .dp(1'b1), .common(1'b1));
  Seven_Seg #(.commonCathode("true"), .commonConnectionType("anode")) seven_seg_4 (
    .a(a3_t), .b(b3_t), .c(c3_t), .d(d3_t), .e(e3), .f(f3), .g(g3), .dp(1'b1), .common(1'b1));
  LED led_3 (.in(1'b1));
  LED led_4 (.in(1'b1));
  Seven_Seg #(.commonCathode("true"), .commonConnectionType("anode")) seven_seg_5 (
    .a(a2_t), .b(b2_t), .c(c2_t), .d(d2_t), .e(e2), .f(f2), .g(g2), .dp(1'b1), .common(1'b1));
  Seven_Seg #(.commonCathode("true"), .commonConnectionType("anode")) seven_seg_6 (
    .a(a1), .b(b1), .c(c1), .d(d1), .e(e1), .f(f1), .g(g1), .dp(1'b1), .common(1'b1));
  // also tied to GND on the sheet: {C6, D6}

  // Other names for the same wires on the sheet: c7[6:0] = out_4; c8[31:0] = out_2; A5 = out_7[0];
  //   horasDerecho[3:0] = out_7; B5 = out_7[1]; C5 = out_7[2]; D5 = out_7[3]; A6 = out_6[0];
  //   horasIzquierda[1:0] = out_6; B6 = out_6[1]; A3 = out_9[0]; minutosDerecho[3:0] = out_9; B3 = out_9[1];
  //   C3 = out_9[2]; D3 = out_9[3]; A4 = out_8[0]; minutosizquierda[3:0] = out_8; B4 = out_8[1]; C4 = out_8[2];
  //   D4 = out_8[3]; A = out_11[0]; segundosDerecho[3:0] = out_11; B = out_11[1]; C = out_11[2]; D = out_11[3];
  //   A2 = out_10[0]; segundosIzquierda[3:0] = out_10; B2 = out_10[1]; C2 = out_10[2]; D2 = out_10[3]
endmodule

/* Code of factorial:
module factorial(
    input [4:0] num,
    input calcular,
    output reg [31:0] Result
);

reg[4:0] i;

always @ (posedge calcular)
begin
    begin
        Result=1;
        i=0;
    end

    for (i = num ; i>0; i--)
    begin
        Result = Result * i ;
    end    
end

endmodule
*/

/* Code of reloj24H:
module reloj24H(
    input clk,
    input minutos,
    input horas,
    output reg [3:0] segundoDer,
    output reg [3:0] segundoIzq,		
    output reg [3:0] minutosDer,
    output reg [3:0] minutosIzq,
    output reg [3:0] horasDiDer,
    output reg [1:0] horasDiIzq
);

initial begin
        segundoDer = 0;
        segundoIzq = 0;
        minutosDer = 0;
        minutosIzq = 0;
        horasDiDer = 0;
        horasDiIzq = 0;
end

always @ (posedge clk) begin
               
        if (segundoDer == 9)
        begin
            segundoDer <= 0;
            segundoIzq = segundoIzq + 1;
            if(segundoIzq == 6)
            begin

                segundoIzq <= 0;
                minutosDer = minutosDer + 1;
                
                if (minutosDer == 10)
                begin
                    minutosDer <= 0;
                    minutosIzq = minutosIzq + 1; // le quitamos el <

                    if(minutosIzq == 6)
                    begin
                        minutosIzq <=0;
                        horasDiDer = horasDiDer +1;
                        if(horasDiDer == 10)
                        begin
                            horasDiDer <=0;
                            horasDiIzq = horasDiIzq + 1;                            
                        end                        
                    end                    
                end

            end                        
        end
        else
        begin
            segundoDer = segundoDer + 1;
        end
        if(horasDiIzq == 2 && horasDiDer ==4)
        begin             
            segundoDer <= 0;
            segundoIzq <= 0;
            minutosDer <= 0;
            minutosIzq <= 0;
            horasDiDer <= 0;
            horasDiIzq <= 0;
        end                                 
end

always @ (posedge minutos) begin
    minutosDer = minutosDer + 1;
    if (minutosDer == 10)
    begin
        minutosDer <= 0;
        minutosIzq = minutosIzq + 1; // le quitamos el <

        if(minutosIzq == 6)
        begin
            minutosIzq <=0;
            horasDiDer = horasDiDer +1;
            if(horasDiDer == 10)
            begin
                horasDiDer <=0;
                horasDiIzq = horasDiIzq + 1;                            
            end                        
        end
    end

    //checks if 24 para que resetee
    if(horasDiIzq == 2 && horasDiDer ==4)
    begin         
        segundoDer <= 0;
        segundoIzq <= 0;
        minutosDer <= 0;
        minutosIzq <= 0;
        horasDiDer <= 0;
        horasDiIzq <= 0;
    end
end

always @ (posedge horas) begin
    horasDiDer = horasDiDer +1;
    if(horasDiDer == 10)
    begin
        horasDiDer <=0;
        horasDiIzq = horasDiIzq + 1;                            
    end

    //checks if 24 para que resetee
    if(horasDiIzq == 2 && horasDiDer ==4)
    begin         
        segundoDer <= 0;
        segundoIzq <= 0;
        minutosDer <= 0;
        minutosIzq <= 0;
        horasDiDer <= 0;
        horasDiIzq <= 0;
    end

end

endmodule
*/

/* Code of cicloFor:
module cicloFor(
    input [4:0] num,
    input calcular,
    output reg [6:0] Result
);

reg[4:0] i;

always @ (posedge calcular)
begin
    begin
        Result=0;
        i=0;
    end

    for (i =0 ; i<=num; i++)
    begin
        Result = Result + i ;
    end    
end

endmodule
*/
