// Digital circuit BoardGame.dig as structural Verilog
module BoardGame (
  input  in_3,
  input  clk,
  input  [4:0] in_17,
  input  [4:0] in_18,
  input  [3:0] in_20,
  output [7:0] out_1,
  output [7:0] out_2,
  output [4:0] out_4,
  output [4:0] out_5,
  output [4:0] out_6,
  output [4:0] out_7,
  output [4:0] out_8,
  output [4:0] out_9,
  output [4:0] out_10,
  output [4:0] out_11,
  output [4:0] out_12,
  output [4:0] out_13,
  output [5:0] out_14,
  output [7:0] out_16,
  output [4:0] out_19,
  output [3:0] out_21,
  output [3:0] out_22,
  output [3:0] out_23,
  output [3:0] out_24,
  output [3:0] out_25
);

  wire a1s9, A2s9, a2s9_t, A3s9, a3s9_t, A4s9, a4s9_t, A5s9, a5s9_t, A6s9, a6s9_t, and_1_out, and_3_out,
       and_4_out, and_6_out, and_7_out, and_8_out, and_9_out, and_10_out, and_13_out, and_14_out, and_15_out,
       and_16_out, and_17_out, and_18_out, and_19_out, and_20_out, and_21_out, and_24_out, and_26_out,
       and_27_out, and_28_out, and_29_out, and_30_out, As9, b0s2, b1s2, b1s9, b2s2, B2s9, b2s9_t, b3s2, B3s9,
       b3s9_t, b4s2, B4s9, b4s9_t, b5s2, B5s9, b5s9_t, b6s2, B6s9, b6s9_t, b7s2, Bs9, button_1_out,
       button_2_out, button_3_out, c1s9, C2s9, c2s9_t, C3s9, c3s9_t, C4s9, c4s9_t, C5s9, c5s9_t, C6s9,
       c6s9_t, clk2s9, clk3s9, clk4s9, clk5s9, clk6s9, comparator_1_eq, comparator_2_eq, comparator_4_eq,
       comparator_6_eq, comparator_8_eq, Cs9, cut2s9, cut3s9, cut4s9, cut5s9, cut6s9, d1s9, D2s9, d2s9_t,
       D3s9, d3s9_t, D4s9, d4s9_t, D5s9, d5s9_t, D6s9, d6s9_t, Ds9, e1s9, e2s9, e3s9, e4s9, e5s9, e6s9,
       en2s9, en3s9, en4s9, en5s9, en6s9, f1s9, f2s9, f3s9, f4s9, f5s9, f6s9, g1s9, g2s9, g3s9, g4s9, g5s9,
       g6s9, multiplexer_1_out, not_4_out, not_7_out, not_8_out, or_1_out, or_2_out, or_3_out, or_4_out,
       or_5_out, or_6_out, or_7_out, Signo, u_RandomGenerator_2_numbergenerated,
       u_RandomGenerator_3_numbergenerated, u_RandomGenerator_4_numbergenerated,
       u_RandomGenerator_5_numbergenerated, u_RandomGenerator_6_numbergenerated,
       u_RandomGenerator_7_numbergenerated, u_RandomGenerator_19_numbergenerated,
       u_RandomGenerator_20_numbergenerated, xor_2_out, xor_4_out, xor_7_out;
  wire [4:0] neg_1_out, neg_2_out, neg_3_out, neg_4_out, neg_5_out, neg_6_out, neg_7_out, neg_8_out,
       neg_9_out, neg_10_out;
  wire [7:0] add_1_s, add_2_s, add_3_s, add_4_s, add_5_s, add_6_s, add_7_s, add_8_s, add_9_s, add_10_s,
       add_11_s, add_12_s, add_13_s, add_14_s, add_15_s, add_16_s, add_17_s, add_18_s, multiplexer_12_out,
       multiplexer_13_out, multiplexer_14_out, multiplexer_15_out, multiplexer_16_out, multiplexer_17_out,
       multiplexer_18_out, multiplexer_19_out, multiplexer_20_out, multiplexer_21_out, multiplexer_22_out,
       multiplexer_23_out, multiplexer_24_out, multiplexer_25_out, multiplexer_26_out, multiplexer_27_out,
       multiplexer_28_out, multiplexer_29_out, multiplexer_30_out, multiplexer_31_out, multiplexer_32_out,
       n1_t, n2_t, n3_t, n4_t, n5_t, n6_t, n7_t, n8_t, n9_t, n10_t, neg_11_out, neg_12_out, neg_13_out,
       neg_14_out, neg_15_out, neg_16_out, neg_17_out, neg_18_out, neg_19_out, neg_20_out, u_ASCII_letra,
       u_HOLA_letra;

  Comparator #(.Bits(4)) comparator_1 (
    .a({D5s9, C5s9, B5s9, A5s9}), .b(4'b0000), .eq(comparator_1_eq));  // open: gt, lt
  and and_1 (and_1_out, A6s9, C6s9);
  and and_2 (clk6s9, en6s9, comparator_1_eq);
  or or_1 (or_1_out, cut6s9, and_1_out);
  _7447 _7447_1 (
    .pin1(B6s9), .pin2(C6s9), .pin3(1'b1), .pin4(1'b1), .pin5(1'b1), .pin6(D6s9), .pin7(A6s9), .pin8(1'b0),
    .pin9(e6s9), .pin10(d6s9_t), .pin11(c6s9_t), .pin12(b6s9_t), .pin13(a6s9_t), .pin14(g6s9), .pin15(f6s9),
    .pin16(1'b1));
  Counter #(.Bits(4)) counter_1 (.en(en6s9), .C(clk6s9), .clr(or_1_out), .out({D6s9, C6s9, B6s9, A6s9}));  // open: ovf
  and and_3 (and_3_out, A5s9, D5s9);
  and and_4 (and_4_out, A5s9, B5s9);
  Comparator #(.Bits(4)) comparator_2 (
    .a({D4s9, C4s9, B4s9, A4s9}), .b(4'b0000), .eq(comparator_2_eq));  // open: gt, lt
  Multiplexer multiplexer_1 (.sel(B6s9), .in_0(and_3_out), .in_1(and_4_out), .out(multiplexer_1_out));
  and and_5 (clk5s9, en5s9, comparator_2_eq);
  or or_2 (or_2_out, cut5s9, multiplexer_1_out);
  _7447 _7447_2 (
    .pin1(B5s9), .pin2(C5s9), .pin3(1'b1), .pin4(1'b1), .pin5(1'b1), .pin6(D5s9), .pin7(A5s9), .pin8(1'b0),
    .pin9(e5s9), .pin10(d5s9_t), .pin11(c5s9_t), .pin12(b5s9_t), .pin13(a5s9_t), .pin14(g5s9), .pin15(f5s9),
    .pin16(1'b1));
  Counter #(.Bits(4)) counter_2 (.en(en5s9), .C(clk5s9), .clr(or_2_out), .out({D5s9, C5s9, B5s9, A5s9}));  // open: ovf
  Counter #(.Bits(4)) counter_3 (.en(cut6s9), .C(clk5s9), .clr(1'b0), .out(out_25));  // open: ovf
  RandomGenerator #(.applicationType("IVERILOG")) u_RandomGenerator (
    .pulse(clk), .numberGenerated({b7s2, b6s2, b5s2, b4s2}));
  Counter #(.Bits(4)) counter_4 (.en(1'b1), .C(clk), .clr(1'b0), .out({b3s2, b2s2, b1s2, b0s2}));  // open: ovf
  Comparator #(.Bits(4)) comparator_3 (.a(out_25), .b(4'b0100), .lt(cut6s9));  // open: gt, eq
  not not_1 (en6s9, cut6s9);
  and and_6 (and_6_out, b1s2, b7s2);
  and and_7 (and_7_out, b1s2, b6s2);
  Comparator #(.Bits(4)) comparator_4 (
    .a({D3s9, C3s9, B3s9, A3s9}), .b(4'b0000), .eq(comparator_4_eq));  // open: gt, lt
  and and_8 (and_8_out, b1s2, b5s2);
  and and_9 (and_9_out, A4s9, C4s9);
  and and_10 (and_10_out, b1s2, b4s2);
  and and_11 (clk4s9, en4s9, comparator_4_eq);
  or or_3 (or_3_out, cut4s9, and_9_out);
  _7447 _7447_3 (
    .pin1(B4s9), .pin2(C4s9), .pin3(1'b1), .pin4(1'b1), .pin5(1'b1), .pin6(D4s9), .pin7(A4s9), .pin8(1'b0),
    .pin9(e4s9), .pin10(d4s9_t), .pin11(c4s9_t), .pin12(b4s9_t), .pin13(a4s9_t), .pin14(g4s9), .pin15(f4s9),
    .pin16(1'b1));
  Counter #(.Bits(4)) counter_5 (.en(en4s9), .C(clk4s9), .clr(or_3_out), .out({D4s9, C4s9, B4s9, A4s9}));  // open: ovf
  Button button_1 (.out(button_1_out));
  Button button_2 (.out(button_2_out));
  Button button_3 (.out(button_3_out));
  and and_12 (out_14[5], or_4_out, and_6_out);
  LED led_1 (.in(out_14[5]));
  Counter #(.Bits(4)) counter_6 (.en(cut5s9), .C(clk4s9), .clr(1'b0), .out(out_24));  // open: ovf
  ARRAY #(.applicationType("IVERILOG")) u_ARRAY (.pos(in_17), .salida(out_16));
  and and_13 (and_13_out, and_14_out, and_7_out);
  or or_4 (or_4_out, and_15_out, and_13_out);
  xor xor_1 (out_14[4], or_4_out, and_6_out);
  LED led_2 (.in(out_14[4]));
  Comparator #(.Bits(4)) comparator_5 (.a(out_24), .b(4'b0100), .lt(cut5s9));  // open: gt, eq
  and and_14 (and_14_out, b0s2, b7s2);
  xor xor_2 (xor_2_out, and_14_out, and_7_out);
  and and_15 (and_15_out, or_5_out, xor_2_out);
  BubbleSort #(.applicationType("IVERILOG")) u_BubbleSort (
    .dato(in_18), .pos(in_20), .almacenar(button_3_out), .ordenar(button_1_out), .show(button_2_out),
    .resultado(out_19));
  and and_16 (and_16_out, and_17_out, and_8_out);
  or or_5 (or_5_out, and_18_out, and_16_out);
  xor xor_3 (out_14[3], or_5_out, xor_2_out);
  LED led_3 (.in(out_14[3]));
  not not_2 (en5s9, cut5s9);
  and and_17 (and_17_out, b0s2, b6s2);
  xor xor_4 (xor_4_out, and_17_out, and_8_out);
  and and_18 (and_18_out, and_19_out, xor_4_out);
  and and_19 (and_19_out, and_10_out, and_20_out);
  xor xor_5 (out_14[2], and_19_out, xor_4_out);
  LED led_4 (.in(out_14[2]));
  Comparator #(.Bits(4)) comparator_6 (
    .a({D2s9, C2s9, B2s9, A2s9}), .b(4'b0000), .eq(comparator_6_eq));  // open: gt, lt
  and and_20 (and_20_out, b0s2, b5s2);
  xor xor_6 (out_14[1], and_20_out, and_10_out);
  LED led_5 (.in(out_14[1]));
  and and_21 (and_21_out, A3s9, D3s9);
  and and_22 (clk3s9, en3s9, comparator_6_eq);
  or or_6 (or_6_out, cut3s9, and_21_out);
  and and_23 (out_14[0], b0s2, b4s2);
  LED led_6 (.in(out_14[0]));
  xor xor_7 (xor_7_out, b3s2, b7s2);
  Counter #(.Bits(4)) counter_7 (.en(en3s9), .C(clk3s9), .clr(or_6_out), .out({D3s9, C3s9, B3s9, A3s9}));  // open: ovf
  _7447 _7447_4 (
    .pin1(B3s9), .pin2(C3s9), .pin3(1'b1), .pin4(1'b1), .pin5(1'b1), .pin6(D3s9), .pin7(A3s9), .pin8(1'b0),
    .pin9(e3s9), .pin10(d3s9_t), .pin11(c3s9_t), .pin12(b3s9_t), .pin13(a3s9_t), .pin14(g3s9), .pin15(f3s9),
    .pin16(1'b1));
  Seven_Seg #(.commonCathode("true"), .commonConnectionType("anode")) seven_seg_1 (
    .a(a6s9_t), .b(b6s9_t), .c(c6s9_t), .d(d6s9_t), .e(e6s9), .f(f6s9), .g(g6s9), .dp(1'b1), .common(1'b1));
  LED B0 (.in(xor_7_out));
  LED B1 (.in(xor_7_out));
  LED B2 (.in(xor_7_out));
  LED B3 (.in(xor_7_out));
  LED B4 (.in(xor_7_out));
  LED B5 (.in(xor_7_out));
  LED B6 (.in(xor_7_out));
  LED B7 (.in(xor_7_out));
  Counter #(.Bits(4)) counter_8 (.en(cut4s9), .C(clk3s9), .clr(1'b0), .out(out_23));  // open: ovf
  Comparator #(.Bits(4)) comparator_7 (.a(out_23), .b(4'b0100), .lt(cut4s9));  // open: gt, eq
  Seven_Seg #(.commonCathode("true"), .commonConnectionType("anode")) seven_seg_2 (
    .a(a5s9_t), .b(b5s9_t), .c(c5s9_t), .d(d5s9_t), .e(e5s9), .f(f5s9), .g(g5s9), .dp(1'b1), .common(1'b1));
  not not_3 (en4s9, cut4s9);
  LED led_7 (.in(1'b1));
  LED led_8 (.in(1'b1));
  Seven_Seg #(.commonCathode("true"), .commonConnectionType("anode")) seven_seg_3 (
    .a(a4s9_t), .b(b4s9_t), .c(c4s9_t), .d(d4s9_t), .e(e4s9), .f(f4s9), .g(g4s9), .dp(1'b1), .common(1'b1));
  Comparator #(.Bits(4)) comparator_8 (.a({Ds9, Cs9, Bs9, As9}), .b(4'b0000), .eq(comparator_8_eq));  // open: gt, lt
  and and_24 (and_24_out, A2s9, C2s9);
  Seven_Seg #(.commonCathode("true"), .commonConnectionType("anode")) seven_seg_4 (
    .a(a3s9_t), .b(b3s9_t), .c(c3s9_t), .d(d3s9_t), .e(e3s9), .f(f3s9), .g(g3s9), .dp(1'b1), .common(1'b1));
  and and_25 (clk2s9, en2s9, comparator_8_eq);
  or or_7 (or_7_out, cut2s9, and_24_out);
  _7447 _7447_5 (
    .pin1(B2s9), .pin2(C2s9), .pin3(1'b1), .pin4(1'b1), .pin5(1'b1), .pin6(D2s9), .pin7(A2s9), .pin8(1'b0),
    .pin9(e2s9), .pin10(d2s9_t), .pin11(c2s9_t), .pin12(b2s9_t), .pin13(a2s9_t), .pin14(g2s9), .pin15(f2s9),
    .pin16(1'b1));
  LED led_9 (.in(1'b1));
  LED led_10 (.in(1'b1));
  Counter #(.Bits(4)) counter_9 (.en(en2s9), .C(clk2s9), .clr(or_7_out), .out({D2s9, C2s9, B2s9, A2s9}));  // open: ovf
  Seven_Seg #(.commonCathode("true"), .commonConnectionType("anode")) seven_seg_5 (
    .a(a2s9_t), .b(b2s9_t), .c(c2s9_t), .d(d2s9_t), .e(e2s9), .f(f2s9), .g(g2s9), .dp(1'b1), .common(1'b1));
  RandomGenerator #(.applicationType("IVERILOG")) u_RandomGenerator_2 (
    .pulse(clk), .numberGenerated(u_RandomGenerator_2_numbergenerated));
  RandomGenerator #(.applicationType("IVERILOG")) u_RandomGenerator_3 (
    .pulse(u_RandomGenerator_2_numbergenerated), .numberGenerated(u_RandomGenerator_3_numbergenerated));
  RandomGenerator #(.applicationType("IVERILOG")) u_RandomGenerator_4 (
    .pulse(u_RandomGenerator_3_numbergenerated), .numberGenerated(u_RandomGenerator_4_numbergenerated));
  RandomGenerator #(.applicationType("IVERILOG")) u_RandomGenerator_5 (
    .pulse(u_RandomGenerator_4_numbergenerated), .numberGenerated(u_RandomGenerator_5_numbergenerated));
  Seven_Seg #(.commonCathode("true"), .commonConnectionType("anode")) seven_seg_6 (
    .a(a1s9), .b(b1s9), .c(c1s9), .d(d1s9), .e(e1s9), .f(f1s9), .g(g1s9), .dp(1'b1), .common(1'b1));
  RandomGenerator #(.applicationType("IVERILOG")) u_RandomGenerator_6 (
    .pulse(clk), .numberGenerated(u_RandomGenerator_6_numbergenerated));
  RandomGenerator #(.applicationType("IVERILOG")) u_RandomGenerator_7 (
    .pulse(clk), .numberGenerated(u_RandomGenerator_7_numbergenerated));
  Counter #(.Bits(4)) counter_10 (.en(cut3s9), .C(clk2s9), .clr(1'b0), .out(out_22));  // open: ovf
  RandomGenerator #(.applicationType("IVERILOG")) u_RandomGenerator_8 (.pulse(clk), .numberGenerated(Signo));
  RandomGenerator #(.applicationType("IVERILOG")) u_RandomGenerator_9 (.pulse(clk), .numberGenerated(out_4));
  RandomGenerator #(.applicationType("IVERILOG")) u_RandomGenerator_10 (.pulse(clk), .numberGenerated(out_5));
  RandomGenerator #(.applicationType("IVERILOG")) u_RandomGenerator_11 (.pulse(clk), .numberGenerated(out_6));
  RandomGenerator #(.applicationType("IVERILOG")) u_RandomGenerator_12 (.pulse(clk), .numberGenerated(out_7));
  Comparator #(.Bits(4)) comparator_9 (.a(out_22), .b(4'b0100), .lt(cut3s9));  // open: gt, eq
  RandomGenerator #(.applicationType("IVERILOG")) u_RandomGenerator_13 (
    .pulse(u_RandomGenerator_2_numbergenerated), .numberGenerated(out_8));
  RandomGenerator #(.applicationType("IVERILOG")) u_RandomGenerator_14 (
    .pulse(u_RandomGenerator_3_numbergenerated), .numberGenerated(out_9));
  RandomGenerator #(.applicationType("IVERILOG")) u_RandomGenerator_15 (
    .pulse(u_RandomGenerator_4_numbergenerated), .numberGenerated(out_10));
  RandomGenerator #(.applicationType("IVERILOG")) u_RandomGenerator_16 (
    .pulse(u_RandomGenerator_5_numbergenerated), .numberGenerated(out_11));
  RandomGenerator #(.applicationType("IVERILOG")) u_RandomGenerator_17 (
    .pulse(u_RandomGenerator_6_numbergenerated), .numberGenerated(out_12));
  RandomGenerator #(.applicationType("IVERILOG")) u_RandomGenerator_18 (.pulse(not_4_out), .numberGenerated(out_13));
  not not_4 (not_4_out, u_RandomGenerator_7_numbergenerated);
  not not_5 (en3s9, cut3s9);
  and and_26 (and_26_out, As9, Ds9);
  Counter #(.Bits(4)) counter_11 (.en(1'b1), .C(clk), .clr(and_26_out), .out({Ds9, Cs9, Bs9, As9}));  // open: ovf
  _7447 _7447_6 (
    .pin1(Bs9), .pin2(Cs9), .pin3(1'b1), .pin4(1'b1), .pin5(1'b1), .pin6(Ds9), .pin7(As9), .pin8(1'b0),
    .pin9(e1s9), .pin10(d1s9), .pin11(c1s9), .pin12(b1s9), .pin13(a1s9), .pin14(g1s9), .pin15(f1s9),
    .pin16(1'b1));
  Counter #(.Bits(4)) counter_12 (.en(cut2s9), .C(clk), .clr(1'b0), .out(out_21));  // open: ovf
  Comparator #(.Bits(4)) comparator_10 (.a(out_21), .b(4'b0100), .lt(cut2s9));  // open: gt, eq
  not not_6 (en2s9, cut2s9);
  not not_7 (not_7_out, in_3);
  Neg #(.Bits(5)) neg_1 (.in(out_4), .out(neg_1_out));
  Neg #(.Bits(5)) neg_2 (.in(out_5), .out(neg_2_out));
  Neg #(.Bits(5)) neg_3 (.in(out_6), .out(neg_3_out));
  Neg #(.Bits(5)) neg_4 (.in(out_7), .out(neg_4_out));
  Neg #(.Bits(5)) neg_5 (.in(out_8), .out(neg_5_out));
  Neg #(.Bits(5)) neg_6 (.in(out_9), .out(neg_6_out));
  Neg #(.Bits(5)) neg_7 (.in(out_10), .out(neg_7_out));
  Neg #(.Bits(5)) neg_8 (.in(out_11), .out(neg_8_out));
  Neg #(.Bits(5)) neg_9 (.in(out_12), .out(neg_9_out));
  Neg #(.Bits(5)) neg_10 (.in(out_13), .out(neg_10_out));
  and and_27 (and_27_out, clk, in_3);
  and and_28 (and_28_out, not_7_out, clk);
  Neg #(.Bits(8)) neg_11 (.in({3'b000, neg_1_out}), .out(neg_11_out));
  Neg #(.Bits(8)) neg_12 (.in({3'b000, neg_2_out}), .out(neg_12_out));
  Neg #(.Bits(8)) neg_13 (.in({3'b000, neg_3_out}), .out(neg_13_out));
  Neg #(.Bits(8)) neg_14 (.in({3'b000, neg_4_out}), .out(neg_14_out));
  Neg #(.Bits(8)) neg_15 (.in({3'b000, neg_5_out}), .out(neg_15_out));
  Neg #(.Bits(8)) neg_16 (.in({3'b000, neg_6_out}), .out(neg_16_out));
  Neg #(.Bits(8)) neg_17 (.in({3'b000, neg_7_out}), .out(neg_17_out));
  Neg #(.Bits(8)) neg_18 (.in({3'b000, neg_8_out}), .out(neg_18_out));
  Neg #(.Bits(8)) neg_19 (.in({3'b000, neg_9_out}), .out(neg_19_out));
  Neg #(.Bits(8)) neg_20 (.in({3'b000, neg_10_out}), .out(neg_20_out));
  Multiplexer #(.Bits(8)) multiplexer_2 (.sel(out_4[4]), .in_0({3'b000, out_4}), .in_1(neg_11_out), .out(n1_t));
  Multiplexer #(.Bits(8)) multiplexer_3 (.sel(out_5[4]), .in_0({3'b000, out_5}), .in_1(neg_12_out), .out(n2_t));
  Multiplexer #(.Bits(8)) multiplexer_4 (.sel(out_6[4]), .in_0({3'b000, out_6}), .in_1(neg_13_out), .out(n3_t));
  Multiplexer #(.Bits(8)) multiplexer_5 (.sel(out_7[4]), .in_0({3'b000, out_7}), .in_1(neg_14_out), .out(n4_t));
  Multiplexer #(.Bits(8)) multiplexer_6 (.sel(out_8[4]), .in_0({3'b000, out_8}), .in_1(neg_15_out), .out(n5_t));
  Multiplexer #(.Bits(8)) multiplexer_7 (.sel(out_9[4]), .in_0({3'b000, out_9}), .in_1(neg_16_out), .out(n6_t));
  Multiplexer #(.Bits(8)) multiplexer_8 (.sel(out_10[4]), .in_0({3'b000, out_10}), .in_1(neg_17_out), .out(n7_t));
  Multiplexer #(.Bits(8)) multiplexer_9 (.sel(out_11[4]), .in_0({3'b000, out_11}), .in_1(neg_18_out), .out(n8_t));
  Multiplexer #(.Bits(8)) multiplexer_10 (.sel(out_12[4]), .in_0({3'b000, out_12}), .in_1(neg_19_out), .out(n9_t));
  Multiplexer #(.Bits(8)) multiplexer_11 (.sel(out_13[4]), .in_0({3'b000, out_13}), .in_1(neg_20_out), .out(n10_t));
  ASCII #(.applicationType("IVERILOG")) u_ASCII (.clockcito(and_27_out), .letra(u_ASCII_letra));
  HOLA #(.applicationType("IVERILOG")) u_HOLA (.clockcito(and_28_out), .letra(u_HOLA_letra));
  Terminal terminal_1 (.D(u_ASCII_letra), .C(and_27_out), .en(1'b1));
  Multiplexer #(.Bits(8)) multiplexer_12 (.sel(n1_t[7]), .in_0(n1_t), .in_1({8{1'b0}}), .out(multiplexer_12_out));
  Multiplexer #(.Bits(8)) multiplexer_13 (.sel(n2_t[7]), .in_0(n2_t), .in_1({8{1'b0}}), .out(multiplexer_13_out));
  Multiplexer #(.Bits(8)) multiplexer_14 (.sel(n3_t[7]), .in_0(n3_t), .in_1({8{1'b0}}), .out(multiplexer_14_out));
  Multiplexer #(.Bits(8)) multiplexer_15 (.sel(n4_t[7]), .in_0(n4_t), .in_1({8{1'b0}}), .out(multiplexer_15_out));
  Multiplexer #(.Bits(8)) multiplexer_16 (.sel(n5_t[7]), .in_0(n5_t), .in_1({8{1'b0}}), .out(multiplexer_16_out));
  Multiplexer #(.Bits(8)) multiplexer_17 (.sel(n6_t[7]), .in_0(n6_t), .in_1({8{1'b0}}), .out(multiplexer_17_out));
  Multiplexer #(.Bits(8)) multiplexer_18 (.sel(n7_t[7]), .in_0(n7_t), .in_1({8{1'b0}}), .out(multiplexer_18_out));
  Multiplexer #(.Bits(8)) multiplexer_19 (.sel(n8_t[7]), .in_0(n8_t), .in_1({8{1'b0}}), .out(multiplexer_19_out));
  Multiplexer #(.Bits(8)) multiplexer_20 (.sel(n9_t[7]), .in_0(n9_t), .in_1({8{1'b0}}), .out(multiplexer_20_out));
  Multiplexer #(.Bits(8)) multiplexer_21 (.sel(n10_t[7]), .in_0(n10_t), .in_1({8{1'b0}}), .out(multiplexer_21_out));
  Multiplexer #(.Bits(8)) multiplexer_22 (.sel(n1_t[7]), .in_0({8{1'b0}}), .in_1(n1_t), .out(multiplexer_22_out));
  Multiplexer #(.Bits(8)) multiplexer_23 (.sel(n2_t[7]), .in_0({8{1'b0}}), .in_1(n2_t), .out(multiplexer_23_out));
  Multiplexer #(.Bits(8)) multiplexer_24 (.sel(n3_t[7]), .in_0({8{1'b0}}), .in_1(n3_t), .out(multiplexer_24_out));
  Multiplexer #(.Bits(8)) multiplexer_25 (.sel(n4_t[7]), .in_0({8{1'b0}}), .in_1(n4_t), .out(multiplexer_25_out));
  Multiplexer #(.Bits(8)) multiplexer_26 (.sel(n5_t[7]), .in_0({8{1'b0}}), .in_1(n5_t), .out(multiplexer_26_out));
  Multiplexer #(.Bits(8)) multiplexer_27 (.sel(n6_t[7]), .in_0({8{1'b0}}), .in_1(n6_t), .out(multiplexer_27_out));
  Multiplexer #(.Bits(8)) multiplexer_28 (.sel(n7_t[7]), .in_0({8{1'b0}}), .in_1(n7_t), .out(multiplexer_28_out));
  Multiplexer #(.Bits(8)) multiplexer_29 (.sel(n8_t[7]), .in_0({8{1'b0}}), .in_1(n8_t), .out(multiplexer_29_out));
  Multiplexer #(.Bits(8)) multiplexer_30 (.sel(n9_t[7]), .in_0({8{1'b0}}), .in_1(n9_t), .out(multiplexer_30_out));
  Multiplexer #(.Bits(8)) multiplexer_31 (.sel(n10_t[7]), .in_0({8{1'b0}}), .in_1(n10_t), .out(multiplexer_31_out));
  Terminal terminal_2 (.D(u_HOLA_letra), .C(and_28_out), .en(1'b1));
  Add #(.Bits(8)) add_1 (.a(multiplexer_12_out), .b(multiplexer_13_out), .c_i(1'b0), .s(add_1_s));  // open: c_o
  Add #(.Bits(8)) add_2 (.a(multiplexer_14_out), .b(multiplexer_15_out), .c_i(1'b0), .s(add_2_s));  // open: c_o
  Add #(.Bits(8)) add_3 (.a(multiplexer_16_out), .b(multiplexer_17_out), .c_i(1'b0), .s(add_3_s));  // open: c_o
  Add #(.Bits(8)) add_4 (.a(multiplexer_18_out), .b(multiplexer_19_out), .c_i(1'b0), .s(add_4_s));  // open: c_o
  Add #(.Bits(8)) add_5 (.a(multiplexer_20_out), .b(multiplexer_21_out), .c_i(1'b0), .s(add_5_s));  // open: c_o
  Add #(.Bits(8)) add_6 (.a(multiplexer_22_out), .b(multiplexer_23_out), .c_i(1'b0), .s(add_6_s));  // open: c_o
  Add #(.Bits(8)) add_7 (.a(multiplexer_24_out), .b(multiplexer_25_out), .c_i(1'b0), .s(add_7_s));  // open: c_o
  Add #(.Bits(8)) add_8 (.a(multiplexer_26_out), .b(multiplexer_27_out), .c_i(1'b0), .s(add_8_s));  // open: c_o
  Add #(.Bits(8)) add_9 (.a(multiplexer_28_out), .b(multiplexer_29_out), .c_i(1'b0), .s(add_9_s));  // open: c_o
  Add #(.Bits(8)) add_10 (.a(multiplexer_30_out), .b(multiplexer_31_out), .c_i(1'b0), .s(add_10_s));  // open: c_o
  Add #(.Bits(8)) add_11 (.a(add_1_s), .b(add_2_s), .c_i(1'b0), .s(add_11_s));  // open: c_o
  Add #(.Bits(8)) add_12 (.a(add_3_s), .b(add_4_s), .c_i(1'b0), .s(add_12_s));  // open: c_o
  Add #(.Bits(8)) add_13 (.a(add_6_s), .b(add_7_s), .c_i(1'b0), .s(add_13_s));  // open: c_o
  Add #(.Bits(8)) add_14 (.a(add_8_s), .b(add_9_s), .c_i(1'b0), .s(add_14_s));  // open: c_o
  Add #(.Bits(8)) add_15 (.a(add_11_s), .b(add_12_s), .c_i(1'b0), .s(add_15_s));  // open: c_o
  Add #(.Bits(8)) add_16 (.a(add_13_s), .b(add_14_s), .c_i(1'b0), .s(add_16_s));  // open: c_o
  RandomGenerator #(.applicationType("IVERILOG")) u_RandomGenerator_19 (
    .pulse(clk), .numberGenerated(u_RandomGenerator_19_numbergenerated));
  not not_8 (not_8_out, Signo);
  Add #(.Bits(8)) add_17 (.a(add_15_s), .b(add_5_s), .c_i(1'b0), .s(add_17_s));  // open: c_o
  RandomGenerator #(.applicationType("IVERILOG")) u_RandomGenerator_20 (
    .pulse(Signo), .numberGenerated(u_RandomGenerator_20_numbergenerated));
  Add #(.Bits(8)) add_18 (.a(add_16_s), .b(add_10_s), .c_i(1'b0), .s(add_18_s));  // open: c_o
  and and_29 (and_29_out, not_8_out, u_RandomGenerator_20_numbergenerated);
  and and_30 (and_30_out, Signo, u_RandomGenerator_19_numbergenerated);
  Multiplexer #(.Bits(8)) multiplexer_32 (
    .sel(and_30_out), .in_0(add_18_s), .in_1({8{1'b0}}), .out(multiplexer_32_out));
  Neg #(.Bits(8)) neg_21 (.in(multiplexer_32_out), .out(out_2));
  Multiplexer #(.Bits(8)) multiplexer_33 (.sel(and_29_out), .in_0(add_17_s), .in_1({8{1'b0}}), .out(out_1));

  // Other names for the same wires on the sheet: N1[4:0] = out_4; N1s9[3:0] = {Ds9, Cs9, Bs9, As9}; N2[4:0] = out_5;
  //   N2s9[3:0] = {D2s9, C2s9, B2s9, A2s9}; N3[4:0] = out_6; N3s9[3:0] = {D3s9, C3s9, B3s9, A3s9}; N4[4:0] = out_7;
  //   N4s9[3:0] = {D4s9, C4s9, B4s9, A4s9}; N5[4:0] = out_8; N5s9[3:0] = {D5s9, C5s9, B5s9, A5s9}; N6[4:0] = out_9;
  //   N6s9[3:0] = {D6s9, C6s9, B6s9, A6s9}; N7[4:0] = out_10; N8[4:0] = out_11; N9[4:0] = out_12; N10[4:0] = out_13;
  //   warp = clk

  // Notes on the sheet:
  //   CAJA NEGRA CA2
endmodule

/* Code of RandomGenerator:
module RandomGenerator(
    input pulse,
    output reg[3:0] numberGenerated
);

initial begin
    numberGenerated = 0;
end

always @ (pulse)
begin
    numberGenerated = $urandom_range(0,4);
end
    
    
endmodule
*/

/* Code of ARRAY:
module ARRAY(
    input [4:0] pos,
    output reg [7:0] salida
);
    //data         //array size
reg [7:0] vector [5:0];

initial begin
    vector [0] = 56;
    vector [1] = 189;
    vector [2] = 190;
    vector [3] = 221;
    vector [4] = 155;
    vector [5] = 235;

end

always @ (*)
begin
    salida = vector[pos];
end

endmodule
*/

/* Code of BubbleSort:
module BubbleSort(
    input [4:0] dato,
    input [3:0] pos,
    input almacenar,
    input ordenar,    
    input show,
    output reg [4:0]resultado
);
    //data         //array size
reg [4:0] vector [15:0];
// temp
reg [4:0] temporal;

//variables para el ciclo 
reg [3:0] i;
reg [3:0] j;

initial begin
    vector [0] = 0;
    vector [1] = 0;
    vector [2] = 0;
    vector [3] = 0;
    vector [4] = 0;
    vector [5] = 0;
    vector [6] = 0;
    vector [7] = 0;
    vector [8] = 0;
    vector [9] = 0;
    vector [10] = 0;
    vector [11] = 0;
    vector [12] = 0;
    vector [13] = 0;
    vector [14] = 0;
    vector [15] = 0;
end

always @ (posedge almacenar) begin
    vector[pos] = dato;
    resultado = vector[pos];
end

always @ (posedge show) begin
    resultado = vector[pos];
end

always @ (pos) begin
    resultado = vector[pos];
end

always @ (posedge ordenar) begin
    
    for (i = 0; i < 16 - 1; i++)
    begin

        // Last i elements are already in place
        for (j = 0; j < 16 - i - 1; j++)
        begin
            if (vector[j] > vector[j + 1])
            begin
                temporal = vector[j];
                vector[j] = vector[j + 1];
                vector[j + 1] = temporal;
                
            end
        end
    end  
end

endmodule
*/

/* Code of RandomGenerator:
module RandomGenerator(
    input pulse,
    output reg numberGenerated
);

initial begin
    numberGenerated = 0;
end

always @ (pulse)
begin
    numberGenerated = $urandom_range(0,1);
end
    
    
endmodule
*/

/* Code of RandomGenerator:
module RandomGenerator(
    input pulse,
    output reg [4:0] numberGenerated
);

initial begin
    numberGenerated = 0;
end

always @ (pulse)
begin
    numberGenerated = $urandom % 31;
end
    
    
endmodule
*/

/* Code of RandomGenerator:
module RandomGenerator(
    input pulse,
    output reg [4:0] numberGenerated
);

initial begin
    numberGenerated = 0;
end

always @ (pulse)
begin
    numberGenerated = $urandom_range(0, 31);
end
    
    
endmodule
*/

/* Code of RandomGenerator:
module RandomGenerator(
    input pulse,
    output reg [4:0] numberGenerated
);

reg [4:0] i;
reg [4:0] j;

initial begin
    numberGenerated = 0;
    i = 0;
    j = 0;
end

always @ (pulse)
begin
    i = $urandom_range(0, 16);
    j = $urandom_range(0, 15);
    numberGenerated = i + j;
end
    
    
endmodule
*/

/* Code of RandomGenerator:
module RandomGenerator(
    input pulse,
    output reg [4:0] numberGenerated
);

reg [4:0] i;
reg [4:0] j;

initial begin
    numberGenerated = 0;
    i = 0;
    j = 0;
end

always @ (pulse)
begin
    i = $urandom_range(0, 8);
    j = $urandom_range(0, 15);
    numberGenerated = (i*2) + j;
end
    
    
endmodule
*/

/* Code of ASCII:
module ASCII(
    input clockcito,
    output reg [7:0] letra
);

//variable de letra
reg [7:0] R;

always @ (posedge clockcito) begin
    
    R = $urandom % 127;
    letra = R;
end
endmodule
*/

/* Code of HOLA:
module HOLA(
    input clockcito,
    output reg [7:0] letra
);

//variable de letra
reg [3:0] R;
initial begin
R = 0;
end

always @ (posedge clockcito) 
begin
    
    if(R == 0)
    begin
        letra = 104;
	    R = 1;
    end

    else if( R == 1)
    begin
        letra = 111;
	    R = 2;
    end

    else if( R == 2)
    begin
        letra = 108;
	R = 3; 
    end

    else if( R == 3)
    begin
        letra = 97;
	R = 4;
    end
    else if ( R == 4)
    begin
        letra = 0;
	R = 4;
    end
    
end
endmodule
*/

/* Code of RandomGenerator:
module RandomGenerator(
    input pulse,
    output reg numberGenerated
);

initial begin
    numberGenerated = 1;
end

always @ (pulse)
begin
    numberGenerated = $urandom_range(0,1);
end
    
    
endmodule
*/
