// Digital circuit CopiadeRelog.dig as structural Verilog
module CopiadeRelog (
  input  clk,
  output [3:0] out_2,
  output [3:0] out_3,
  output [3:0] out_4,
  output [3:0] out_5,
  output [3:0] out_6
);

  wire A, a1, A2, a2_t, A3, a3_t, A4, a4_t, A5, a5_t, A6, a6_t, and_1_out, and_3_out, and_4_out, and_6_out,
       and_8_out, and_10_out, and_12_out, B, b1, B2, b2_t, B3, b3_t, B4, b4_t, B5, b5_t, B6, b6_t, C, c1, C2,
       c2_t, C3, c3_t, C4, c4_t, C5, c5_t, C6, c6_t, clk2, clk3, clk4, clk5, clk6, comparator_1_eq,
       comparator_2_eq, comparator_4_eq, comparator_6_eq, comparator_8_eq, cut2, cut3, cut4, cut5, cut6, D,
       d1, D2, d2_t, D3, d3_t, D4, d4_t, D5, d5_t, D6, d6_t, e1, e2, e3, e4, e5, e6, en2, en3, en4, en5, en6,
       f1, f2, f3, f4, f5, f6, g1, g2, g3, g4, g5, g6, multiplexer_1_out, or_1_out, or_2_out, or_3_out,
       or_4_out, or_5_out;

  Comparator #(.Bits(4)) comparator_1 (.a({D5, C5, B5, A5}), .b(4'b0000), .eq(comparator_1_eq));  // open: gt, lt
  and and_1 (and_1_out, A6, C6);
  and and_2 (clk6, en6, comparator_1_eq);
  or or_1 (or_1_out, cut6, and_1_out);
  _7447 _7447_1 (
    .pin1(B6), .pin2(C6), .pin3(1'b1), .pin4(1'b1), .pin5(1'b1), .pin6(D6), .pin7(A6), .pin8(1'b0),
    .pin9(e6), .pin10(d6_t), .pin11(c6_t), .pin12(b6_t), .pin13(a6_t), .pin14(g6), .pin15(f6), .pin16(1'b1));
  Counter #(.Bits(4)) counter_1 (.en(en6), .C(clk6), .clr(or_1_out), .out({D6, C6, B6, A6}));  // open: ovf
  and and_3 (and_3_out, A5, D5);
  and and_4 (and_4_out, A5, B5);
  Comparator #(.Bits(4)) comparator_2 (.a({D4, C4, B4, A4}), .b(4'b0000), .eq(comparator_2_eq));  // open: gt, lt
  Multiplexer multiplexer_1 (.sel(B6), .in_0(and_3_out), .in_1(and_4_out), .out(multiplexer_1_out));
  and and_5 (clk5, en5, comparator_2_eq);
  or or_2 (or_2_out, cut5, multiplexer_1_out);
  Counter #(.Bits(4)) counter_2 (.en(en5), .C(clk5), .clr(or_2_out), .out({D5, C5, B5, A5}));  // open: ovf
  _7447 _7447_2 (
    .pin1(B5), .pin2(C5), .pin3(1'b1), .pin4(1'b1), .pin5(1'b1), .pin6(D5), .pin7(A5), .pin8(1'b0),
    .pin9(e5), .pin10(d5_t), .pin11(c5_t), .pin12(b5_t), .pin13(a5_t), .pin14(g5), .pin15(f5), .pin16(1'b1));
  Counter #(.Bits(4)) counter_3 (.en(cut6), .C(clk5), .clr(1'b0), .out(out_6));  // open: ovf
  Comparator #(.Bits(4)) comparator_3 (.a(out_6), .b(4'b0100), .lt(cut6));  // open: gt, eq
  not not_1 (en6, cut6);
  Comparator #(.Bits(4)) comparator_4 (.a({D3, C3, B3, A3}), .b(4'b0000), .eq(comparator_4_eq));  // open: gt, lt
  and and_6 (and_6_out, A4, C4);
  and and_7 (clk4, en4, comparator_4_eq);
  or or_3 (or_3_out, cut4, and_6_out);
  _7447 _7447_3 (
    .pin1(B4), .pin2(C4), .pin3(1'b1), .pin4(1'b1), .pin5(1'b1), .pin6(D4), .pin7(A4), .pin8(1'b0),
    .pin9(e4), .pin10(d4_t), .pin11(c4_t), .pin12(b4_t), .pin13(a4_t), .pin14(g4), .pin15(f4), .pin16(1'b1));
  Counter #(.Bits(4)) counter_4 (.en(en4), .C(clk4), .clr(or_3_out), .out({D4, C4, B4, A4}));  // open: ovf
  Counter #(.Bits(4)) counter_5 (.en(cut5), .C(clk4), .clr(1'b0), .out(out_5));  // open: ovf
  Comparator #(.Bits(4)) comparator_5 (.a(out_5), .b(4'b0100), .lt(cut5));  // open: gt, eq
  not not_2 (en5, cut5);
  Comparator #(.Bits(4)) comparator_6 (.a({D2, C2, B2, A2}), .b(4'b0000), .eq(comparator_6_eq));  // open: gt, lt
  and and_8 (and_8_out, A3, D3);
  and and_9 (clk3, en3, comparator_6_eq);
  or or_4 (or_4_out, cut3, and_8_out);
  Counter #(.Bits(4)) counter_6 (.en(en3), .C(clk3), .clr(or_4_out), .out({D3, C3, B3, A3}));  // open: ovf
  _7447 _7447_4 (
    .pin1(B3), .pin2(C3), .pin3(1'b1), .pin4(1'b1), .pin5(1'b1), .pin6(D3), .pin7(A3), .pin8(1'b0),
    .pin9(e3), .pin10(d3_t), .pin11(c3_t), .pin12(b3_t), .pin13(a3_t), .pin14(g3), .pin15(f3), .pin16(1'b1));
  Counter #(.Bits(4)) counter_7 (.en(cut4), .C(clk3), .clr(1'b0), .out(out_4));  // open: ovf
  Seven_Seg #(.commonCathode("true"), .commonConnectionType("anode")) seven_seg_1 (
    .a(a6_t), .b(b6_t), .c(c6_t), .d(d6_t), .e(e6), .f(f6), .g(g6), .dp(1'b1), .common(1'b1));
  Comparator #(.Bits(4)) comparator_7 (.a(out_4), .b(4'b0100), .lt(cut4));  // open: gt, eq
  Seven_Seg #(.commonCathode("true"), .commonConnectionType("anode")) seven_seg_2 (
    .a(a5_t), .b(b5_t), .c(c5_t), .d(d5_t), .e(e5), .f(f5), .g(g5), .dp(1'b1), .common(1'b1));
  not not_3 (en4, cut4);
  LED led_1 (.in(1'b1));
  LED led_2 (.in(1'b1));
  Seven_Seg #(.commonCathode("true"), .commonConnectionType("anode")) seven_seg_3 (
    .a(a4_t), .b(b4_t), .c(c4_t), .d(d4_t), .e(e4), .f(f4), .g(g4), .dp(1'b1), .common(1'b1));
  Comparator #(.Bits(4)) comparator_8 (.a({D, C, B, A}), .b(4'b0000), .eq(comparator_8_eq));  // open: gt, lt
  Seven_Seg #(.commonCathode("true"), .commonConnectionType("anode")) seven_seg_4 (
    .a(a3_t), .b(b3_t), .c(c3_t), .d(d3_t), .e(e3), .f(f3), .g(g3), .dp(1'b1), .common(1'b1));
  and and_10 (and_10_out, A2, C2);
  and and_11 (clk2, en2, comparator_8_eq);
  or or_5 (or_5_out, cut2, and_10_out);
  LED led_3 (.in(1'b1));
  LED led_4 (.in(1'b1));
  _7447 _7447_5 (
    .pin1(B2), .pin2(C2), .pin3(1'b1), .pin4(1'b1), .pin5(1'b1), .pin6(D2), .pin7(A2), .pin8(1'b0),
    .pin9(e2), .pin10(d2_t), .pin11(c2_t), .pin12(b2_t), .pin13(a2_t), .pin14(g2), .pin15(f2), .pin16(1'b1));
  Seven_Seg #(.commonCathode("true"), .commonConnectionType("anode")) seven_seg_5 (
    .a(a2_t), .b(b2_t), .c(c2_t), .d(d2_t), .e(e2), .f(f2), .g(g2), .dp(1'b1), .common(1'b1));
  Counter #(.Bits(4)) counter_8 (.en(en2), .C(clk2), .clr(or_5_out), .out({D2, C2, B2, A2}));  // open: ovf
  Seven_Seg #(.commonCathode("true"), .commonConnectionType("anode")) seven_seg_6 (
    .a(a1), .b(b1), .c(c1), .d(d1), .e(e1), .f(f1), .g(g1), .dp(1'b1), .common(1'b1));
  Counter #(.Bits(4)) counter_9 (.en(cut3), .C(clk2), .clr(1'b0), .out(out_3));  // open: ovf
  Comparator #(.Bits(4)) comparator_9 (.a(out_3), .b(4'b0100), .lt(cut3));  // open: gt, eq
  not not_4 (en3, cut3);
  and and_12 (and_12_out, A, D);
  Counter #(.Bits(4)) counter_10 (.en(1'b1), .C(clk), .clr(and_12_out), .out({D, C, B, A}));  // open: ovf
  _7447 _7447_6 (
    .pin1(B), .pin2(C), .pin3(1'b1), .pin4(1'b1), .pin5(1'b1), .pin6(D), .pin7(A), .pin8(1'b0), .pin9(e1),
    .pin10(d1), .pin11(c1), .pin12(b1), .pin13(a1), .pin14(g1), .pin15(f1), .pin16(1'b1));
  Counter #(.Bits(4)) counter_11 (.en(cut2), .C(clk), .clr(1'b0), .out(out_2));  // open: ovf
  Comparator #(.Bits(4)) comparator_10 (.a(out_2), .b(4'b0100), .lt(cut2));  // open: gt, eq
  not not_5 (en2, cut2);

  // Other names for the same wires on the sheet: N1[3:0] = {D, C, B, A}; N2[3:0] = {D2, C2, B2, A2};
  //   N3[3:0] = {D3, C3, B3, A3}; N4[3:0] = {D4, C4, B4, A4}; N5[3:0] = {D5, C5, B5, A5}; N6[3:0] = {D6, C6, B6, A6}
endmodule
