// Digital circuit ExamenII.dig as structural Verilog
module ExamenII (
  input  shift,
  input  clk,
  input  start,
  input  clk_2,
  output [9:0] out_5
);

  wire a_out, clck, comparator_1_eq, e_out, i_out, not_1_out, o_out, start_t, u_out, u_writer_finescribir;
  wire [2:0] u_POSITION_salida;
  wire [3:0] position;
  wire [5:0] multiplexer_1_out;
  wire [7:0] a, e, i, multiplexer_2_out, o, u, u_writer_salida;
  wire [9:0] add_1_s;

  not not_1 (not_1_out, comparator_1_eq);
  and and_1 (clck, clk, not_1_out);
  Counter #(.Bits(4)) counter_1 (.en(1'b1), .C(clck), .clr(1'b0), .out(position));  // open: ovf
  Multiplexer #(.Selector_Bits(4), .Bits(6)) multiplexer_1 (
    .sel(position), .in_0(6'b000111), .in_1(6'b000110), .in_2(6'b000111), .in_3(6'b000110), .in_4(6'b000101),
    .in_5(6'b000111), .in_6(6'b000101), .in_7(6'b000001), .in_8(6'b001001), .in_9(6'b000110),
    .in_10(6'b000111), .in_11(6'b000110), .in_12(6'b000101), .in_13(6'b000111), .in_14(6'b000101),
    .in_15(6'b000001), .out(multiplexer_1_out));
  Comparator #(.Bits(6)) comparator_1 (.a(6'b001001), .b(multiplexer_1_out), .eq(comparator_1_eq));  // open: gt, lt
  Add #(.Bits(10)) add_1 (.a(out_5), .b({4'b0000, multiplexer_1_out}), .c_i(1'b0), .s(add_1_s));  // open: c_o
  Button u_a (.out(a_out));
  Button u_e (.out(e_out));
  Button u_i (.out(i_out));
  Button u_o (.out(o_out));
  Button u_u (.out(u_out));
  letraA #(.applicationType("IVERILOG")) u_letraA (.tecla(a_out), .caps(shift), .letra(a));
  letraE #(.applicationType("IVERILOG")) u_letraE (.tecla(e_out), .caps(shift), .letra(e));
  letraI #(.applicationType("IVERILOG")) u_letraI (.tecla(i_out), .caps(shift), .letra(i));
  letraO #(.applicationType("IVERILOG")) u_letraO (.tecla(o_out), .caps(shift), .letra(o));
  letraU #(.applicationType("IVERILOG")) u_letraU (.tecla(u_out), .caps(shift), .letra(u));
  and and_2 (start_t, start, clk_2);
  Register #(.Bits(10)) register_1 (.D(add_1_s), .C(clck), .en(1'b1), .Q(out_5));
  POSITION #(.applicationType("IVERILOG")) u_POSITION (
    .entrada1(a), .entrada2(e), .entrada3(i), .entrada4(o), .entrada5(u), .salida(u_POSITION_salida));
  Multiplexer #(.Selector_Bits(3), .Bits(8)) multiplexer_2 (
    .sel(u_POSITION_salida), .in_0(a), .in_1(e), .in_2(i), .in_3(o), .in_4(u), .in_5({8{1'b0}}),
    .in_6({8{1'b0}}), .in_7({8{1'b0}}), .out(multiplexer_2_out));
  writer #(.applicationType("IVERILOG")) u_writer (
    .start(start_t), .entrada(multiplexer_2_out), .clear(u_writer_finescribir), .salida(u_writer_salida),
    .finescribir(u_writer_finescribir));
  Terminal terminal_1 (.D(u_writer_salida), .C(start_t), .en(1'b1));
endmodule

/* Code of letraA:
module letraA(
    input tecla,
    input caps,
    output reg [7:0]letra
);

reg [7:0] a;
reg [7:0] A;

initial begin 
    a = 97;
    A = 65;
end

always @ (posedge tecla)
begin
    if(caps)
    begin
        letra = A;
    end
    else
    begin
        letra = a;
    end
end

endmodule
*/

/* Code of letraE:
module letraE(
    input tecla,
    input caps,
    output reg [7:0]letra
);

reg [7:0] e;
reg [7:0] E;

initial begin 
    e = 101;
    E = 69;
end

always @ (posedge tecla)
begin
    if(caps)
    begin
        letra = E;
    end
    else
    begin
        letra = e;
    end
end

endmodule
*/

/* Code of letraI:
module letraI(
    input tecla,
    input caps,
    output reg [7:0]letra
);

reg [7:0] i;
reg [7:0] I;

initial begin 
    i = 105;
    I = 73;
end

always @ (posedge tecla)
begin
    if(caps)
    begin
        letra = I;
    end
    else
    begin
        letra = i;
    end
end

endmodule
*/

/* Code of letraO:
module letraO(
    input tecla,
    input caps,
    output reg [7:0]letra
);

reg [7:0] o;
reg [7:0] O;

initial begin 
    o = 111;
    O = 79;
end

always @ (posedge tecla)
begin
    if(caps)
    begin
        letra = O;
    end
    else
    begin
        letra = o;
    end
end
endmodule
*/

/* Code of letraU:
module letraU(
    input tecla,
    input caps,
    output reg [7:0]letra
);

reg [7:0] u;
reg [7:0] U;

initial begin 
    u = 117;
    U = 85;
end

always @ (posedge tecla)
begin
    if(caps)
    begin
        letra = U;
    end
    else
    begin
        letra = u;
    end
end

endmodule
*/

/* Code of POSITION:
module POSITION(
    input [7:0] entrada1,
    input [7:0] entrada2,
    input [7:0] entrada3,
    input [7:0] entrada4,
    input [7:0] entrada5,
    output reg [2:0] salida
);


initial begin    
    salida = 0;
end

always @ (posedge entrada1)
begin
    salida = 0;
 end

always @ (posedge entrada2)
begin
    salida = 1;
end

always @ (posedge entrada3)
begin
    salida = 2;
end

always @ (posedge entrada4)
begin
    salida = 3;
end

always @ (posedge entrada5)
begin
    salida = 4;
end

endmodule
*/

/* Code of writer:
module writer(
    input start,
    input [7:0] entrada,    
    input clear,		    
    output reg [7:0] salida,
    output reg finescribir
);

    //data         //array size
reg [7:0] data [4:0];
reg [3:0] i;
reg [3:0] j;


initial begin
    salida = 0;
    i = 0;
    j=0;
    data [0] = 0;
    data [1] = 0;
    data [2] = 0;
    data [3] = 0;
    data [4] = 0;
    finescribir = 0;
end


always @ (entrada)
begin
    data [i] = entrada;
    ++i;
    if(i==5)
    begin
        i=0;
    end
end

always @ (posedge start)
begin
    salida = data [j];
    ++j;
    if(j==5)
    begin
        j=0;
        finescribir = 1;
    end
end

always @ (posedge finescribir)
begin
    salida = 0;
    i = 0;
    j=0;
    data [0] = 0;
    data [1] = 0;
    data [2] = 0;
    data [3] = 0;
    data [4] = 0;
    finescribir = 0;
end

endmodule
*/
