// Digital circuit Reloj24HProyecto.dig as structural Verilog
module Reloj24HProyecto (
  input  clk,
  output [3:0] out_2,
  output [3:0] out_3,
  output [3:0] out_4,
  output [3:0] out_5,
  output [3:0] out_6
);

  wire a1s9, A2s9, a2s9_t, A3s9, a3s9_t, A4s9, a4s9_t, A5s9, a5s9_t, A6s9, a6s9_t, and_1_out, and_3_out,
       and_4_out, and_6_out, and_8_out, and_10_out, and_12_out, As9, b1s9, B2s9, b2s9_t, B3s9, b3s9_t, B4s9,
       b4s9_t, B5s9, b5s9_t, B6s9, b6s9_t, Bs9, c1s9, C2s9, c2s9_t, C3s9, c3s9_t, C4s9, c4s9_t, C5s9, c5s9_t,
       C6s9, c6s9_t, clk2s9, clk3s9, clk4s9, clk5s9, clk6s9, comparator_1_eq, comparator_2_eq,
       comparator_4_eq, comparator_6_eq, comparator_8_eq, Cs9, cut2s9, cut3s9, cut4s9, cut5s9, cut6s9, d1s9,
       D2s9, d2s9_t, D3s9, d3s9_t, D4s9, d4s9_t, D5s9, d5s9_t, D6s9, d6s9_t, Ds9, e1s9, e2s9, e3s9, e4s9,
       e5s9, e6s9, en2s9, en3s9, en4s9, en5s9, en6s9, f1s9, f2s9, f3s9, f4s9, f5s9, f6s9, g1s9, g2s9, g3s9,
       g4s9, g5s9, g6s9, multiplexer_1_out, or_1_out, or_2_out, or_3_out, or_4_out, or_5_out;

  Comparator #(.Bits(4)) comparator_1 (
    .a({D5s9, C5s9, B5s9, A5s9}), .b(4'b0000), .eq(comparator_1_eq));  // open: gt, lt
  and and_1 (and_1_out, A6s9, C6s9);
  and and_2 (clk6s9, en6s9, comparator_1_eq);
  or or_1 (or_1_out, cut6s9, and_1_out);
  _7447 _7447_1 (
    .pin1(B6s9), .pin2(C6s9), .pin3(1'b1), .pin4(1'b1), .pin5(1'b1), .pin6(D6s9), .pin7(A6s9), .pin8(1'b0),
    .pin9(e6s9), .pin10(d6s9_t), .pin11(c6s9_t), .pin12(b6s9_t), .pin13(a6s9_t), .pin14(g6s9), .pin15(f6s9),
    .pin16(1'b1));
  Counter #(.Bits(4)) counter_1 (.en(en6s9), .C(clk6s9), .clr(or_1_out), .out({D6s9, C6s9, B6s9, A6s9}));  // open: ovf
  and and_3 (and_3_out, A5s9, D5s9);
  and and_4 (and_4_out, A5s9, B5s9);
  Comparator #(.Bits(4)) comparator_2 (
    .a({D4s9, C4s9, B4s9, A4s9}), .b(4'b0000), .eq(comparator_2_eq));  // open: gt, lt
  Multiplexer multiplexer_1 (.sel(B6s9), .in_0(and_3_out), .in_1(and_4_out), .out(multiplexer_1_out));
  and and_5 (clk5s9, en5s9, comparator_2_eq);
  or or_2 (or_2_out, cut5s9, multiplexer_1_out);
  Counter #(.Bits(4)) counter_2 (.en(en5s9), .C(clk5s9), .clr(or_2_out), .out({D5s9, C5s9, B5s9, A5s9}));  // open: ovf
  _7447 _7447_2 (
    .pin1(B5s9), .pin2(C5s9), .pin3(1'b1), .pin4(1'b1), .pin5(1'b1), .pin6(D5s9), .pin7(A5s9), .pin8(1'b0),
    .pin9(e5s9), .pin10(d5s9_t), .pin11(c5s9_t), .pin12(b5s9_t), .pin13(a5s9_t), .pin14(g5s9), .pin15(f5s9),
    .pin16(1'b1));
  Counter #(.Bits(4)) counter_3 (.en(cut6s9), .C(clk5s9), .clr(1'b0), .out(out_6));  // open: ovf
  Comparator #(.Bits(4)) comparator_3 (.a(out_6), .b(4'b0100), .lt(cut6s9));  // open: gt, eq
  not not_1 (en6s9, cut6s9);
  Comparator #(.Bits(4)) comparator_4 (
    .a({D3s9, C3s9, B3s9, A3s9}), .b(4'b0000), .eq(comparator_4_eq));  // open: gt, lt
  and and_6 (and_6_out, A4s9, C4s9);
  and and_7 (clk4s9, en4s9, comparator_4_eq);
  or or_3 (or_3_out, cut4s9, and_6_out);
  _7447 _7447_3 (
    .pin1(B4s9), .pin2(C4s9), .pin3(1'b1), .pin4(1'b1), .pin5(1'b1), .pin6(D4s9), .pin7(A4s9), .pin8(1'b0),
    .pin9(e4s9), .pin10(d4s9_t), .pin11(c4s9_t), .pin12(b4s9_t), .pin13(a4s9_t), .pin14(g4s9), .pin15(f4s9),
    .pin16(1'b1));
  Counter #(.Bits(4)) counter_4 (.en(en4s9), .C(clk4s9), .clr(or_3_out), .out({D4s9, C4s9, B4s9, A4s9}));  // open: ovf
  Counter #(.Bits(4)) counter_5 (.en(cut5s9), .C(clk4s9), .clr(1'b0), .out(out_5));  // open: ovf
  Comparator #(.Bits(4)) comparator_5 (.a(out_5), .b(4'b0100), .lt(cut5s9));  // open: gt, eq
  not not_2 (en5s9, cut5s9);
  Comparator #(.Bits(4)) comparator_6 (
    .a({D2s9, C2s9, B2s9, A2s9}), .b(4'b0000), .eq(comparator_6_eq));  // open: gt, lt
  and and_8 (and_8_out, A3s9, D3s9);
  and and_9 (clk3s9, en3s9, comparator_6_eq);
  or or_4 (or_4_out, cut3s9, and_8_out);
  Counter #(.Bits(4)) counter_6 (.en(en3s9), .C(clk3s9), .clr(or_4_out), .out({D3s9, C3s9, B3s9, A3s9}));  // open: ovf
  _7447 _7447_4 (
    .pin1(B3s9), .pin2(C3s9), .pin3(1'b1), .pin4(1'b1), .pin5(1'b1), .pin6(D3s9), .pin7(A3s9), .pin8(1'b0),
    .pin9(e3s9), .pin10(d3s9_t), .pin11(c3s9_t), .pin12(b3s9_t), .pin13(a3s9_t), .pin14(g3s9), .pin15(f3s9),
    .pin16(1'b1));
  Counter #(.Bits(4)) counter_7 (.en(cut4s9), .C(clk3s9), .clr(1'b0), .out(out_4));  // open: ovf
  Seven_Seg #(.commonCathode("true"), .commonConnectionType("anode")) seven_seg_1 (
    .a(a6s9_t), .b(b6s9_t), .c(c6s9_t), .d(d6s9_t), .e(e6s9), .f(f6s9), .g(g6s9), .dp(1'b1), .common(1'b1));
  Comparator #(.Bits(4)) comparator_7 (.a(out_4), .b(4'b0100), .lt(cut4s9));  // open: gt, eq
  Seven_Seg #(.commonCathode("true"), .commonConnectionType("anode")) seven_seg_2 (
    .a(a5s9_t), .b(b5s9_t), .c(c5s9_t), .d(d5s9_t), .e(e5s9), .f(f5s9), .g(g5s9), .dp(1'b1), .common(1'b1));
  not not_3 (en4s9, cut4s9);
  LED led_1 (.in(1'b1));
  LED led_2 (.in(1'b1));
  Seven_Seg #(.commonCathode("true"), .commonConnectionType("anode")) seven_seg_3 (
    .a(a4s9_t), .b(b4s9_t), .c(c4s9_t), .d(d4s9_t), .e(e4s9), .f(f4s9), .g(g4s9), .dp(1'b1), .common(1'b1));
  Comparator #(.Bits(4)) comparator_8 (.a({Ds9, Cs9, Bs9, As9}), .b(4'b0000), .eq(comparator_8_eq));  // open: gt, lt
  Seven_Seg #(.commonCathode("true"), .commonConnectionType("anode")) seven_seg_4 (
    .a(a3s9_t), .b(b3s9_t), .c(c3s9_t), .d(d3s9_t), .e(e3s9), .f(f3s9), .g(g3s9), .dp(1'b1), .common(1'b1));
  and and_10 (and_10_out, A2s9, C2s9);
  and and_11 (clk2s9, en2s9, comparator_8_eq);
  or or_5 (or_5_out, cut2s9, and_10_out);
  LED led_3 (.in(1'b1));
  LED led_4 (.in(1'b1));
  _7447 _7447_5 (
    .pin1(B2s9), .pin2(C2s9), .pin3(1'b1), .pin4(1'b1), .pin5(1'b1), .pin6(D2s9), .pin7(A2s9), .pin8(1'b0),
    .pin9(e2s9), .pin10(d2s9_t), .pin11(c2s9_t), .pin12(b2s9_t), .pin13(a2s9_t), .pin14(g2s9), .pin15(f2s9),
    .pin16(1'b1));
  Seven_Seg #(.commonCathode("true"), .commonConnectionType("anode")) seven_seg_5 (
    .a(a2s9_t), .b(b2s9_t), .c(c2s9_t), .d(d2s9_t), .e(e2s9), .f(f2s9), .g(g2s9), .dp(1'b1), .common(1'b1));
  Counter #(.Bits(4)) counter_8 (.en(en2s9), .C(clk2s9), .clr(or_5_out), .out({D2s9, C2s9, B2s9, A2s9}));  // open: ovf
  Seven_Seg #(.commonCathode("true"), .commonConnectionType("anode")) seven_seg_6 (
    .a(a1s9), .b(b1s9), .c(c1s9), .d(d1s9), .e(e1s9), .f(f1s9), .g(g1s9), .dp(1'b1), .common(1'b1));
  Counter #(.Bits(4)) counter_9 (.en(cut3s9), .C(clk2s9), .clr(1'b0), .out(out_3));  // open: ovf
  Comparator #(.Bits(4)) comparator_9 (.a(out_3), .b(4'b0100), .lt(cut3s9));  // open: gt, eq
  not not_4 (en3s9, cut3s9);
  and and_12 (and_12_out, As9, Ds9);
  Counter #(.Bits(4)) counter_10 (.en(1'b1), .C(clk), .clr(and_12_out), .out({Ds9, Cs9, Bs9, As9}));  // open: ovf
  _7447 _7447_6 (
    .pin1(Bs9), .pin2(Cs9), .pin3(1'b1), .pin4(1'b1), .pin5(1'b1), .pin6(Ds9), .pin7(As9), .pin8(1'b0),
    .pin9(e1s9), .pin10(d1s9), .pin11(c1s9), .pin12(b1s9), .pin13(a1s9), .pin14(g1s9), .pin15(f1s9),
    .pin16(1'b1));
  Counter #(.Bits(4)) counter_11 (.en(cut2s9), .C(clk), .clr(1'b0), .out(out_2));  // open: ovf
  Comparator #(.Bits(4)) comparator_10 (.a(out_2), .b(4'b0100), .lt(cut2s9));  // open: gt, eq
  not not_5 (en2s9, cut2s9);

  // Other names for the same wires on the sheet: N1s9[3:0] = {Ds9, Cs9, Bs9, As9};
  //   N2s9[3:0] = {D2s9, C2s9, B2s9, A2s9}; N3s9[3:0] = {D3s9, C3s9, B3s9, A3s9};
  //   N4s9[3:0] = {D4s9, C4s9, B4s9, A4s9}; N5s9[3:0] = {D5s9, C5s9, B5s9, A5s9};
  //   N6s9[3:0] = {D6s9, C6s9, B6s9, A6s9}
endmodule
